# Fritzing sketch v1.4.5 (gnd) (saved by Fritzing 0.9.4)
circuit board: 10cm x 10cm

parts:
  Arduino_Mega_2560 = Arduino Mega 2560 (Rev3) [part_number="Arduino Mega 2560"]
  Q1 = Basic FET N-Channel [part_number=STP62NS04Z package="TO220 [THT]"]
  Q2 = Basic FET N-Channel [part_number=STP62NS04Z package="TO220 [THT]"]
  Q3 = Basic FET N-Channel [part_number=STP62NS04Z package="TO220 [THT]"]
  Q4 = Basic FET N-Channel [part_number=STP62NS04Z package="TO220 [THT]"]
  D15 = Schottky Diode [part_number=1N5818 package="300 mil [THT]"]
  U2 = V18ZA2P [part_number=ERZV14D220 package=v18za2p]
  IC3 = IC, DIP package, 8 pins [chip_label="Dual VR Conditioner"]
  JP1 = female pin header, 3 pins [form="♀ (female)"]
  JP3 = female pin header, 3 pins [form="♀ (female)"]
  JP5 = female pin header, 2 pins [form="♀ (female)"]
  Q5 = Basic FET N-Channel [part_number=STP62NS04Z package="TO220 [THT]"]
  Q7 = Basic FET N-Channel [part_number=STP62NS04Z package="TO220 [THT]"]
  Q6 = Basic FET N-Channel [part_number=STP62NS04Z package="TO220 [THT]"]
  Q8 = Basic FET N-Channel [part_number=STP62NS04Z package="TO220 [THT]"]
  DRV8825 = Pololu A4988 [package=SO16]
  J142 = female pin header, 3 pins [form="♀ (female)"]
  C5 = Ceramic Capacitor [capacitance=0.1µF package="0805 [SMD, multilayer]"]
  C20 = Ceramic Capacitor [capacitance=1µF package="0805 [SMD, multilayer]"]
  C12 = Ceramic Capacitor [capacitance=1µF package="0805 [SMD, multilayer]"]
  C4 = Ceramic Capacitor [capacitance=0.22µF package="0805 [SMD, multilayer]"]
  R62 = Resistor [tolerance=±5% resistance=120 package="0805 [SMD]"]
  C2 = Ceramic Capacitor [capacitance=0.22µF package="0805 [SMD, multilayer]"]
  C1 = Ceramic Capacitor [capacitance=0.1µF package="0805 [SMD, multilayer]"]
  R7 = Resistor [tolerance=±0.1% resistance=3.9k package="0805 [SMD]"]
  R1 = Resistor [tolerance=±0.1% resistance=2.49k package="0805 [SMD]"]
  C8 = Ceramic Capacitor [capacitance=0.22µF package="0805 [SMD, multilayer]"]
  C7 = Ceramic Capacitor [capacitance=0.1µF package="0805 [SMD, multilayer]"]
  R59 = Resistor [tolerance=±5% resistance=220 package="0805 [SMD]"]
  R40 = Resistor [tolerance=±5% resistance=1k package="0805 [SMD]"]
  R39 = Resistor [tolerance=±5% resistance=1k package="0805 [SMD]"]
  R60 = Resistor [tolerance=±5% resistance=1k package="0805 [SMD]"]
  C24 = Ceramic Capacitor [capacitance=100nF package="0805 [SMD, multilayer]"]
  R3 = Resistor [tolerance=±0.1% resistance=2.49k package="0805 [SMD]"]
  C10 = Ceramic Capacitor [capacitance=0.22µF package="0805 [SMD, multilayer]"]
  C9 = Ceramic Capacitor [capacitance=0.1µF package="0805 [SMD, multilayer]"]
  C25 = Ceramic Capacitor [capacitance=0.01µF package="0805 [SMD, multilayer]"]
  C3 = Ceramic Capacitor [capacitance=0.1µF package="0805 [SMD, multilayer]"]
  R2 = Resistor [tolerance=±5% resistance=470 package="0805 [SMD]"]
  R4 = Resistor [tolerance=±5% resistance=470 package="0805 [SMD]"]
  R54 = Resistor [tolerance=±5% resistance=10k package="0805 [SMD]"]
  R22 = Resistor [tolerance=±5% resistance=470 package="0805 [SMD]"]
  R6 = Resistor [tolerance=±5% resistance=470 package="0805 [SMD]"]
  C6 = Ceramic Capacitor [capacitance=0.22µF package="0805 [SMD, multilayer]"]
  R31 = Resistor [tolerance=±5% resistance=10 power=1 package="0805 [SMD]"]
  R32 = Resistor [tolerance=±5% resistance=10 power=2W package="0805 [SMD]"]
  R8 = Resistor [tolerance=±5% resistance=470 package="0805 [SMD]"]
  R21 = Resistor [tolerance=±5% resistance=1k package="0805 [SMD]"]
  R49 = Resistor [tolerance=±5% resistance=100k power=0.25W package="0805 [SMD]"]
  R55 = Resistor [tolerance=±5% resistance=100k package="0805 [SMD]"]
  R48 = Resistor [tolerance=±5% resistance=100k package="0805 [SMD]"]
  R56 = Resistor [tolerance=±5% resistance=100k power=0.25W package="0805 [SMD]"]
  R51 = Resistor [tolerance=±5% resistance=1k package="0805 [SMD]"]
  R57 = Resistor [tolerance=±5% resistance=1k package="0805 [SMD]"]
  R50 = Resistor [tolerance=±5% resistance=1k package="0805 [SMD]"]
  R58 = Resistor [tolerance=±5% resistance=1k package="0805 [SMD]"]
  R27 = Resistor [tolerance=±5% resistance=10 power=2W package="0805 [SMD]"]
  R25 = Resistor [tolerance=±5% resistance=10 power=2W package="0805 [SMD]"]
  R35 = Resistor [tolerance=±5% resistance=100k package="0805 [SMD]"]
  R37 = Resistor [tolerance=±5% resistance=100k package="0805 [SMD]"]
  R23 = Resistor [tolerance=±5% resistance=1k package="0805 [SMD]"]
  R24 = Resistor [tolerance=±5% resistance=1k package="0805 [SMD]"]
  C11 = Ceramic Capacitor [capacitance=1µF package="0805 [SMD, multilayer]"]
  R38 = Resistor [tolerance=±5% resistance=100k package="0805 [SMD]"]
  R29 = Resistor [tolerance=±5% resistance=1k package="0805 [SMD]"]
  R30 = Resistor [tolerance=±5% resistance=1k package="0805 [SMD]"]
  R36 = Resistor [tolerance=±5% resistance=100k package="0805 [SMD]"]
  R9 = Resistor [tolerance=±5% resistance=100k package="0805 [SMD]"]
  R12 = Resistor [tolerance=±5% resistance=1k power=0.25W package="0805 [SMD]"]
  R10 = Resistor [tolerance=±5% resistance=100k power=0.25W package="0805 [SMD]"]
  R11 = Resistor [tolerance=±5% resistance=1k package="0805 [SMD]"]
  R13 = Resistor [tolerance=±5% resistance=100k package="0805 [SMD]"]
  R15 = Resistor [tolerance=±5% resistance=1k package="0805 [SMD]"]
  R14 = Resistor [tolerance=±5% resistance=100k package="0805 [SMD]"]
  R16 = Resistor [tolerance=±5% resistance=1k package="0805 [SMD]"]
  R41 = Resistor [tolerance=±5% resistance=470 package="0805 [SMD]"]
  C19 = Ceramic Capacitor [capacitance=0.01µF package="0805 [SMD, multilayer]"]
  R61 = Resistor [tolerance=±5% resistance=2.49k package="0805 [SMD]"]
  C15 = Ceramic Capacitor [capacitance=0.1µF voltage=50V package="0805 [SMD, multilayer]"]
  C13 = Ceramic Capacitor [capacitance=0.1µF voltage=50V package="0805 [SMD, multilayer]"]
  D16 = Schottky Diode [part_number=1N5818 package="300 mil [THT]"]
  R63 = Resistor [tolerance=±5% resistance=10k package="0805 [SMD]"]
  C26 = Ceramic Capacitor [capacitance=0.1µF package="0805 [SMD, multilayer]"]
  R64 = Resistor [tolerance=±5% resistance=470 package="0805 [SMD]"]
  C27 = Ceramic Capacitor [capacitance=0.22µF package="0805 [SMD, multilayer]"]
  C28 = Ceramic Capacitor [capacitance=0.1µF package="0805 [SMD, multilayer]"]
  R65 = Resistor [tolerance=±5% resistance=470 package="0805 [SMD]"]
  C29 = Ceramic Capacitor [capacitance=0.22µF package="0805 [SMD, multilayer]"]
  C23 = Ceramic Capacitor [capacitance=22µF package="0805 [SMD, multilayer]"]
  U4 = RS485 [package=so08]
  316370-6 = TE_Con_316370-6_040_II SRS_MK-II_48Pin_CAP-ASSY [part_number=316370-6 package="48-pin 0.040\" 3 row"]
  C18 = Ceramic Capacitor [capacitance=10pF package="0805 [SMD, multilayer]"]
  IC6 = ULN2003A [package="SO16 [SMD]"]
  J145 = female pin header, 8 pins [form="♀ (female)"]  # not connected
  J146 = female pin header, 8 pins [form="♀ (female)"]  # not connected
  J147 = female pin header, 8 pins [form="♀ (female)"]  # not connected
  JP2 = female pin header, 3 pins [form="♀ (female)"]
  GND = female pin header, 3 pins [form="♀ (female)"]
  5V = female pin header, 3 pins [form="♀ (female)"]
  C14 = Tantalum Capacitor [capacitance=47µF voltage=10V package="200 mil [THT, tantalum]"]
  JP4 = female pin header, 2 pins [form="♀ (female)"]
  IC2 = IC, DIP package, 8 pins [chip_label=IC]
  IC1 = IC, DIP package, 8 pins [chip_label=IC]
  U1 = Voltage Regulator - 5V [package="TO220 [THT]"]
  IC4 = IC, DIP package, 8 pins [chip_label=SP720]
  IC5 = IC, DIP package, 8 pins [chip_label=SP720]
  J148 = female pin header, 6 pins [form="♀ (female)"]
  C16 = Tantalum Capacitor [capacitance=10µF voltage=35V package="A 3216 [SMD, tantalum]"]
  C30 = Ceramic Capacitor [capacitance=0.22µF package="0805 [SMD, multilayer]"]

nets:
  ADC Clamp1/O2-CPU-A8: Arduino_Mega_2560.A8, C10.1, R22.Pin_1, IC4.pin3
  ADC Clamp6/IAT-CPU-A0: Arduino_Mega_2560.A0, C2.1, R2.Pin_1, IC5.pin2
  ADC Clamp2/CLT-CPU-A1: Arduino_Mega_2560.A1, C4.1, R4.Pin_1, IC5.pin1
  ADC Clamp3/TPS-CPU-A2: Arduino_Mega_2560.A2, R6.Pin_1, C6.1, IC4.pin7
  ACD Clamp8/MAP-CPU-A3: Arduino_Mega_2560.A3, R41.Pin_1, 316370-6.1P, C18.0, IC4.pin6
  ADC Clamp4/BRV-CPU-A4: Arduino_Mega_2560.A4, C8.0, R8.Pin_1, IC4.pin5
  FuelPress-A5: Arduino_Mega_2560.A5, R64.Pin_1, C27.1
  OilPress-A7: Arduino_Mega_2560.A7, R65.Pin_1, C29.1
  SCL-CPU-D21: Arduino_Mega_2560.D21/SCL
  ADC Clamp5/TACH1-CPU-D19: Arduino_Mega_2560.D19/RX1, IC3.pin8, R59.Pin_1, C25.1, IC4.pin1
  ADC Clamp7/TACH2-CPU-D18: Arduino_Mega_2560.D18/TX1, IC3.pin7, R60.Pin_1, C24.0, IC4.pin2
  STEP-CPU-D17: Arduino_Mega_2560.D17_PWM/RX2, DRV8825.STEP
  STEPDIR-CPU-D16: Arduino_Mega_2560.D16_PWM/TX2, DRV8825.DIR
  SDA-CPU-D20: Arduino_Mega_2560.SDA
  GND: Arduino_Mega_2560.GND, Q1.source, Q2.source, Q3.source, Q4.source, U2.P$2, IC3.pin6, Q5.source, Q7.source, Q6.source, Q8.source, DRV8825.GND, C5.0, C20.0, C12.0, C4.0, C2.0, C1.0, C8.1, C7.0, C24.1, C10.0, C9.0, C25.0, C3.0, C6.0, R21.Pin_1, R49.Pin_0, R55.Pin_0, R48.Pin_0, R56.Pin_0, R35.Pin_0, R37.Pin_0, C11.0, R38.Pin_0, R36.Pin_0, R9.Pin_1, R10.Pin_1, R13.Pin_1, R14.Pin_1, C19.0, C15.0, C13.0, D16.cathode, C26.0, C27.0, C28.0, C29.0, C23.1, U4.DE, 316370-6.1K, 316370-6.1M, 316370-6.2E, 316370-6.2H, 316370-6.2I, 316370-6.2M, 316370-6.2O, C18.1, IC6.0V, GND.pin1, GND.pin2, GND.pin3, C14.-, IC2.pin3, IC1.pin3, U1.GND, IC4.pin4, IC5.pin4, J148.pin3, C16.-, C30.0
  INJ4-CPU-D11: Arduino_Mega_2560.D11_PWM, R14.Pin_0, R16.Pin_0
  INJ3-CPU-D10: Arduino_Mega_2560.D10_PWM, R13.Pin_0, R15.Pin_0
  INJ2-CPU-D9: Arduino_Mega_2560.D9_PWM, R12.Pin_0, R10.Pin_0
  INJ1-CPU-D8: Arduino_Mega_2560.D8_PWM, R9.Pin_0, R11.Pin_0
  RESET: Arduino_Mega_2560.RESET, J142.pin2
  5V: Arduino_Mega_2560.5V, IC3.pin5, JP1.pin3, DRV8825.RESET, DRV8825.SLEEP, C20.1, R62.Pin_1, R1.Pin_0, R40.Pin_0, R39.Pin_0, R3.Pin_0, R54.Pin_1, C19.1, R61.Pin_1, C13.1, D16.anode, U4._RE, 316370-6.1T, 316370-6.1U, 316370-6.1V, 316370-6.1W, 316370-6.1X, 5V.pin1, 5V.pin2, 5V.pin3, C14.+, U1.output_voltage, IC4.pin8, IC5.pin8, J148.pin2
  RX: Arduino_Mega_2560.D0_RX0, J148.pin4
  TX: Arduino_Mega_2560.D1_TX0, J148.pin5
  ACD Clamp9/CPU-D2/Flex: Arduino_Mega_2560.D2_PWM, R61.Pin_0, 316370-6.2Q, IC5.pin7, C30.1
  CPU-D4: Arduino_Mega_2560.D4_PWM, R58.Pin_0
  CPU-D5: Arduino_Mega_2560.D5_PWM, R50.Pin_0
  CPU-D6: Arduino_Mega_2560.D6_PWM, R57.Pin_0
  CPU-D7: Arduino_Mega_2560.D7_PWM, R51.Pin_0
  CPU-D24: Arduino_Mega_2560.D24, DRV8825.ENABLE
  IGN2-CPU-D24: Arduino_Mega_2560.D38, R24.Pin_0
  IGN1-CPU-D28: Arduino_Mega_2560.D40, R23.Pin_0
  RST-CPU-D48: Arduino_Mega_2560.D43, IC6.In_2
  LC-CPU-D45: Arduino_Mega_2560.D45, IC6.In_4
  LC-CPU-D47: Arduino_Mega_2560.D47, IC6.In_3
  LC-CPU-D49: Arduino_Mega_2560.D49, IC6.In_5
  IGN4-CPU-D36: Arduino_Mega_2560.D50, R30.Pin_0
  LC-5-OUT/LC-CPU-D51: Arduino_Mega_2560.D51, 316370-6.1H
  IGN3-CPU-D40: Arduino_Mega_2560.D52, R29.Pin_0
  N1: Q1.gate, R11.Pin_1
  INJ-1-OUT: Q1.drain, 316370-6.2V
  N2: Q2.gate, R15.Pin_1
  INJ-3-OUT: Q2.drain, 316370-6.2U
  N3: Q3.gate, R12.Pin_1
  INJ-2-OUT: Q3.drain, 316370-6.2X
  N4: Q4.gate, R16.Pin_1
  INJ-4-OUT: Q4.drain, 316370-6.2W
  N5: D15.cathode, U1.input_voltage
  12V/12V-raw: D15.anode, U2.P$1, JP1.pin1, DRV8825.VMOT, R7.Pin_0, C15.1, R63.Pin_1, 316370-6.2R, IC6.COM_-_Common, C16.+
  VR1-: IC3.pin1, 316370-6.1R
  N6: IC3.pin2, JP2.pin3
  N7: IC3.pin3, JP3.pin1
  VR2-: IC3.pin4, 316370-6.1Q
  JP1-OUT: JP1.pin2, C12.1, C11.1, IC2.pin6, IC1.pin6
  VR2+: JP3.pin2, JP5.pin1, 316370-6.1O
  N8: JP3.pin3, R60.Pin_0
  N9: JP5.pin2, R40.Pin_1
  N10: Q5.gate, R55.Pin_1, R57.Pin_1
  HC-1-OUT: Q5.drain, 316370-6.2P
  N11: Q7.gate, R48.Pin_1, R50.Pin_1
  IDLE-OUT: Q7.drain, 316370-6.2N
  N12: Q6.gate, R56.Pin_1, R58.Pin_1
  HC-2-OUT: Q6.drain, 316370-6.2L
  N13: Q8.gate, R49.Pin_1, R51.Pin_1
  BOOST-OUT: Q8.drain, 316370-6.2S
  STEP-1B-OUT: DRV8825.1B, 316370-6.2G
  STEP-1A-OUT: DRV8825.1A, 316370-6.2D
  STEP-2A-OUT: DRV8825.2A, 316370-6.2A
  STEP-2B-OUT: DRV8825.2B, 316370-6.2B
  N14: J142.pin1, R54.Pin_0
  N15: J142.pin3, R62.Pin_0, C23.0
  TPS Sensor: C5.1, R6.Pin_0, 316370-6.1G
  IAT Sensor: C1.1, R1.Pin_1, R2.Pin_0, 316370-6.1L
  N16: R7.Pin_1, C7.1, R8.Pin_0, R21.Pin_0
  N17: R59.Pin_0, JP2.pin1
  N18: R39.Pin_1, JP4.pin1
  CLT Sensor: R3.Pin_1, C3.1, R4.Pin_0, 316370-6.1J
  O2 Sensor: C9.1, R22.Pin_0, 316370-6.1B
  IGN-3-OUT: R31.Pin_0, 316370-6.2C
  N19: R31.Pin_1, IC2.pin7
  N20: R32.Pin_0, IC2.pin5
  IGN-4-OUT: R32.Pin_1, 316370-6.2F
  IGN-1-OUT: R27.Pin_0, 316370-6.2J
  N21: R27.Pin_1, IC1.pin7
  N22: R25.Pin_0, IC1.pin5
  IGN-2-OUT: R25.Pin_1, 316370-6.2K
  N23: R35.Pin_1, R24.Pin_1, IC1.pin4
  N24: R37.Pin_1, R23.Pin_1, IC1.pin2
  N25: R38.Pin_1, R29.Pin_1, IC2.pin2
  N26: R30.Pin_1, R36.Pin_1, IC2.pin4
  EXT-MAP: R41.Pin_0, U4.DI, 316370-6.1S
  LC-4-OUT: R63.Pin_0, 316370-6.1I, IC6.Out_5
  FuelPress: C26.1, R64.Pin_0, 316370-6.1D
  OilPress: C28.1, R65.Pin_0, 316370-6.1A
  LC-2-OUT: 316370-6.1C, IC6.Out_3
  LC-1-OUT: 316370-6.1E, IC6.Out_2
  LC-3-OUT: 316370-6.1F, IC6.Out_4
  VR1+: 316370-6.1N, JP2.pin2, JP4.pin2

notes:
  Inlet Air Temperature sensor
  Coolant Temperature Sensor
  Speeduino v0.4, Throttle Position Sensor
  Battery Reference Voltage
  Injector 1
  Speeduino v0.4, Connector 1
  Injector 3
  Injector 2
  Injector 4
  Speeduino v0.4, O2 Sensor
  Ignitor output 1
  12v
  5v
  Power supply
  IGN Out
  Crank and Cam sensors
  Speeduino v0.4, MAP sensor input
  DetonationEMS.com
  Generic Outputs - High Current
  inj1
  VR
  Hall
  Reset Protection - Refer AVR040 Application note
  Stepper Driver
  PWM Idle / Boost
  Proto Area
  Run  Prog
  Aaron S. 2020
  Flex-Fuel  Input
  ULN2003a
  TX RX
  GND VCC
  PreIgnition v0.1

custom parts:
  TE_Con_316370-6_040_II SRS_MK-II_48Pin_CAP-ASSY: TE Connectors_316370-6_040_II SRS_MK-II_48Pin_CAP-ASSY
