# Fritzing sketch v1.0.0.0.0 (saved by Fritzing 0.9.4)
breadboards: 1

parts:
  C11 = Ceramic Capacitor [capacitance=0.1µF package="0805 [SMD, multilayer]"]
  C12 = Ceramic Capacitor [capacitance=0.22µF package="0805 [SMD, multilayer]"]
  R23 = Resistor [tolerance=±5% resistance=470 package="0805 [SMD]"]
  C13 = Ceramic Capacitor [capacitance=0.1µF package="0805 [SMD, multilayer]"]
  C14 = Ceramic Capacitor [capacitance=0.22µF package="0805 [SMD, multilayer]"]
  R24 = Resistor [tolerance=±5% resistance=470 package="0805 [SMD]"]
  J1 = female pin header, 3 pins [form="♀ (female)"]

nets:
  GND: C11.0, C12.0, C13.0, C14.0
  Aux1: C11.1, R23.Pin_0, J1.pin1
  A5: C12.1, R23.Pin_1
  Aux2: C13.1, R24.Pin_0, J1.pin2
  A6: C14.1, R24.Pin_1

notes:
  Speeduino v0.4, Aux1
  Speeduino v0.4, Aux2
  Speeduino v0.4, Output
