# Fritzing sketch Universal v1.0 (input diode) (saved by Fritzing 0.9.4)
circuit board: 10cm x 2.5cm

parts:
  1 = shrouded pin header, 40 pins [form="♂ (shrouded male)"]
  J4 = female pin header, 20 pins [form="♀ (female)"]
  J5 = female pin header, 20 pins [form="♀ (female)"]
  12v_GND = screw terminal, 2 pins
  GND_12v = screw terminal, 2 pins
  D1 = Rectifier Diode [part_number=1N4001 package="300 mil [THT]"]
  D2 = Rectifier Diode [part_number=1N4001 package="300 mil [THT]"]
  J6 = female pin header, 3 pins [form="♀ (female)"]
  J7 = female pin header, 3 pins [form="♀ (female)"]

nets (from the pcb view):
  N1: 1.pin1, J4.pin20
  N2: 1.pin2, J4.pin19
  N3: 1.pin3, J4.pin18
  N4: 1.pin4, J4.pin17
  N5: 1.pin5, J4.pin16
  N6: 1.pin6, J4.pin15
  N7: 1.pin7, J4.pin14
  N8: 1.pin8, J4.pin13
  N9: 1.pin11, J4.pin10
  N10: 1.pin13, 1.pin28, J4.pin8, J5.pin8
  N11: 1.pin14, J4.pin7
  N12: 1.pin15, J4.pin6
  N13: 1.pin16, J4.pin5
  N14: 1.pin17, J4.pin4
  N15: 1.pin18, J4.pin3
  N16: 1.pin19, J4.pin2
  N17: 1.pin20, J4.pin1
  N18: 1.pin21, J5.pin1
  N19: 1.pin22, J5.pin2
  N20: 1.pin24, D2.anode, J7.pin3
  N21: 1.pin25, D1.anode, J6.pin3
  N22: 1.pin26, J5.pin6
  N23: 1.pin27, J5.pin7
  N24: 1.pin29, J5.pin9
  N25: 1.pin30, J5.pin10
  N26: 1.pin31, J5.pin11
  N27: 1.pin32, J5.pin12
  N28: 1.pin33, J5.pin13
  N29: 1.pin34, J5.pin14
  N30: 1.pin35, J5.pin15
  N31: 1.pin36, J5.pin16
  N32: 1.pin37, J5.pin17
  N33: 1.pin38, J5.pin18
  N34: 1.pin39, J5.pin19
  N35: 1.pin40, J5.pin20
  N36: J5.pin4, J7.pin2
  N37: J5.pin5, J6.pin2
  N38: 12v_GND.pin2, GND_12v.pin2
  N39: D1.cathode, J6.pin1
  N40: D2.cathode, J7.pin1

notes:
  Speeduino v0.4, Connector 1
  inj1
  Aaron S. 2020
  DetonationEMS.com
  20
  21
  40
  1
  Cam
  Crank
  1 2 3
  Jumper CKP/CMP
  2-3=12v Hall
  1-2=5v Hall or VR
