# Fritzing sketch IGNC v0.1.3 (saved by Fritzing 0.9.4)
circuit board: 4cm x 1.1cm
breadboards: 1

parts:
  Q2 = Basic FET N-Channel-flat [package="TO220 [THT]"]
  Q3 = Basic FET N-Channel-flat [package="TO220 [THT]"]
  Q4 = Basic FET N-Channel-flat [package="TO220 [THT]"]
  J2 = female pin header, 9 pins [form="♀ (female)"]

nets:
  N1: Q2.1, J2.pin9
  N2: Q2.2, J2.pin8
  N3: Q3.1, J2.pin7
  N4: Q3.2, J2.pin6
  N5: Q4.1, J2.pin5
  N6: Q4.2, J2.pin4
  N7: J2.pin1, J2.pin2, J2.pin3

notes:
  In Out In Out In Out GND GND GND
  Detonation Spark v1.3
  Aaron S. 2019
  In Out GND

custom parts:
  Basic FET N-Channel-flat: MOSFET N-Channel Transistor lying flat on PCB. 16.7mm from mounting hole centre to leg hole centres.
