# Fritzing sketch IGNC v0.1.4 (saved by Fritzing 0.9.4)
circuit board: 5cm x 1.1cm
breadboards: 1

parts:
  Q1 = Basic FET N-Channel-flat [package="TO220 [THT]"]
  Q2 = Basic FET N-Channel-flat [package="TO220 [THT]"]
  Q3 = Basic FET N-Channel-flat [package="TO220 [THT]"]
  Q4 = Basic FET N-Channel-flat [package="TO220 [THT]"]
  J2 = female pin header, 12 pins [form="♀ (female)"]

nets:
  N1: Q1.1, J2.pin12
  N2: Q1.2, J2.pin11
  N3: Q2.1, J2.pin10
  N4: Q2.2, J2.pin9
  N5: Q3.1, J2.pin8
  N6: Q3.2, J2.pin7
  N7: Q4.1, J2.pin6
  N8: Q4.2, J2.pin5
  N9: J2.pin1, J2.pin2, J2.pin3, J2.pin4

notes:
  In Out In Out In Out In Out
  Detonation Spark v1.4
  Aaron S. 2019
  In Out GND
  GND GND GND GND

custom parts:
  Basic FET N-Channel-flat: MOSFET N-Channel Transistor lying flat on PCB. 16.7mm from mounting hole centre to leg hole centres.
