# Fritzing sketch IGNC-2 (35x15mm) (saved by Fritzing 0.9.4)
circuit board: 3.5cm x 1.5cm
breadboards: 1

parts:
  Q2 = Basic FET N-Channel-flat [package="TO220 [THT]"]
  Q4 = Basic FET N-Channel-flat [package="TO220 [THT]"]
  J2 = female pin header, 6 pins [form="♀ (female)"]

nets:
  N1: Q2.1, J2.pin6
  N2: Q2.2, J2.pin5
  GND: Q2.3, Q4.3, J2.pin3, J2.pin4
  N3: Q4.1, J2.pin2
  N4: Q4.2, J2.pin1

notes:
  ECU
  DetonationEMS.com
  Aaron S. 2020
  Coil
  | GND |
  IGN2
  IGN1

custom parts:
  Basic FET N-Channel-flat: MOSFET N-Channel Transistor lying flat on PCB. 16.7mm from mounting hole centre to leg hole centres.
