# Fritzing sketch IGNC (saved by Fritzing 0.9.3b)
circuit board: 6cm x 4cm
breadboards: 1

parts:
  IG1 = MOSFET-NCHANNEL [package=to220v]
  IG2 = MOSFET-NCHANNEL [package=to220v]
  IG3 = MOSFET-NCHANNEL [package=to220v]
  IG4 = MOSFET-NCHANNEL [package=to220v]
  ENGINE_GROUND = Screw terminal - 2 pins [package=THT]
  ECU_IN = screw terminal, 4 pins
  Coil_Out = screw terminal, 4 pins
  R1 = Resistor [tolerance=±5% resistance=330 package=THT]
  R2 = Resistor [tolerance=±5% resistance=330 package=THT]
  R3 = Resistor [tolerance=±5% resistance=330 package=THT]
  R4 = Resistor [tolerance=±5% resistance=330 package=THT]

nets:
  N1: IG1.G, R1.Pin_1
  N2: IG1.D, Coil_Out.pin1
  N3: IG1.S, IG2.S, IG3.S, IG4.S, ENGINE_GROUND.pin1, ENGINE_GROUND.pin2
  N4: IG2.G, R3.Pin_1
  N5: IG2.D, Coil_Out.pin2
  N6: IG3.G, R2.Pin_1
  N7: IG3.D, Coil_Out.pin3
  N8: IG4.G, R4.Pin_1
  N9: IG4.D, Coil_Out.pin4
  N10: ECU_IN.pin1, R1.Pin_0
  N11: ECU_IN.pin2, R3.Pin_0
  N12: ECU_IN.pin3, R2.Pin_0
  N13: ECU_IN.pin4, R4.Pin_0

notes:
  1  2  3  4
  Detonation Spark v0.1
  Aaron S. 2019
  (G)(OUT)(IN)
