# Fritzing sketch v1.0.0 (saved by Fritzing 0.9.4)
circuit board: 10cm x 10cm

parts:
  Q1 = Basic FET N-Channel [part_number=STP62NS04Z package="TO220 [THT]"]
  Q2 = Basic FET N-Channel [part_number=STP62NS04Z package="TO220 [THT]"]
  Q3 = Basic FET N-Channel [part_number=STP62NS04Z package="TO220 [THT]"]
  Q4 = Basic FET N-Channel [part_number=STP62NS04Z package="TO220 [THT]"]
  U1 = Voltage Regulator - 5V [part_number=LM2940T-5.0 package="TO220 [THT]"]
  D15 = Schottky Diode [part_number=1N5818 package="300 mil [THT]"]
  U2 = V18ZA2P [part_number=ERZV14D220 package=v18za2p]
  IC3 = IC, DIP package, 8 pins [chip_label="Dual VR Conditioner"]
  JP1 = female pin header, 3 pins [form="♀ (female)"]
  JP2 = female pin header, 3 pins [form="♀ (female)"]
  JP3 = female pin header, 3 pins [form="♀ (female)"]
  JP4 = female pin header, 2 pins [form="♀ (female)"]
  JP5 = female pin header, 2 pins [form="♀ (female)"]
  Q5 = Basic FET N-Channel [part_number=STP62NS04Z package="TO220 [THT]"]
  Q7 = Basic FET N-Channel [part_number=STP62NS04Z package="TO220 [THT]"]
  Q6 = Basic FET N-Channel [part_number=STP62NS04Z package="TO220 [THT]"]
  Q8 = Basic FET N-Channel [part_number=STP62NS04Z package="TO220 [THT]"]
  DRV8825 = Pololu A4988 [package=SO16]
  J142 = female pin header, 3 pins [form="♀ (female)"]
  C5 = Ceramic Capacitor [capacitance=0.1µF package="0805 [SMD, multilayer]"]
  C20 = Ceramic Capacitor [capacitance=1µF package="0805 [SMD, multilayer]"]
  C12 = Ceramic Capacitor [capacitance=1µF package="0805 [SMD, multilayer]"]
  C4 = Ceramic Capacitor [capacitance=0.22µF package="0805 [SMD, multilayer]"]
  R62 = Resistor [tolerance=±5% resistance=120 package="0805 [SMD]"]
  C2 = Ceramic Capacitor [capacitance=0.22µF package="0805 [SMD, multilayer]"]
  C1 = Ceramic Capacitor [capacitance=0.1µF package="0805 [SMD, multilayer]"]
  R7 = Resistor [tolerance=±0.1% resistance=3.9k package="0805 [SMD]"]
  R1 = Resistor [tolerance=±0.1% resistance=2.49k package="0805 [SMD]"]
  C8 = Ceramic Capacitor [capacitance=0.22µF package="0805 [SMD, multilayer]"]
  C7 = Ceramic Capacitor [capacitance=0.1µF package="0805 [SMD, multilayer]"]
  R59 = Resistor [tolerance=±5% resistance=220 package="0805 [SMD]"]
  R40 = Resistor [tolerance=±5% resistance=1k package="0805 [SMD]"]
  R39 = Resistor [tolerance=±5% resistance=1k package="0805 [SMD]"]
  R60 = Resistor [tolerance=±5% resistance=1k package="0805 [SMD]"]
  C24 = Ceramic Capacitor [capacitance=100nF package="0805 [SMD, multilayer]"]
  R3 = Resistor [tolerance=±0.1% resistance=2.49k package="0805 [SMD]"]
  C10 = Ceramic Capacitor [capacitance=0.22µF package="0805 [SMD, multilayer]"]
  C9 = Ceramic Capacitor [capacitance=0.1µF package="0805 [SMD, multilayer]"]
  C25 = Ceramic Capacitor [capacitance=0.01µF package="0805 [SMD, multilayer]"]
  C3 = Ceramic Capacitor [capacitance=0.1µF package="0805 [SMD, multilayer]"]
  R2 = Resistor [tolerance=±5% resistance=470 package="0805 [SMD]"]
  R4 = Resistor [tolerance=±5% resistance=470 package="0805 [SMD]"]
  R54 = Resistor [tolerance=±5% resistance=10k package="0805 [SMD]"]
  R22 = Resistor [tolerance=±5% resistance=470 package="0805 [SMD]"]
  R6 = Resistor [tolerance=±5% resistance=470 package="0805 [SMD]"]
  C6 = Ceramic Capacitor [capacitance=0.22µF package="0805 [SMD, multilayer]"]
  R31 = Resistor [tolerance=±5% resistance=10 power=1 package="0805 [SMD]"]
  R32 = Resistor [tolerance=±5% resistance=10 power=2W package="0805 [SMD]"]
  R8 = Resistor [tolerance=±5% resistance=470 package="0805 [SMD]"]
  R21 = Resistor [tolerance=±5% resistance=1k package="0805 [SMD]"]
  R49 = Resistor [tolerance=±5% resistance=100k power=0.25W package="0805 [SMD]"]
  R55 = Resistor [tolerance=±5% resistance=100k package="0805 [SMD]"]
  R48 = Resistor [tolerance=±5% resistance=100k package="0805 [SMD]"]
  R56 = Resistor [tolerance=±5% resistance=100k power=0.25W package="0805 [SMD]"]
  R51 = Resistor [tolerance=±5% resistance=1k package="0805 [SMD]"]
  R57 = Resistor [tolerance=±5% resistance=1k package="0805 [SMD]"]
  R50 = Resistor [tolerance=±5% resistance=1k package="0805 [SMD]"]
  R58 = Resistor [tolerance=±5% resistance=1k package="0805 [SMD]"]
  R27 = Resistor [tolerance=±5% resistance=10 power=2W package="0805 [SMD]"]
  R25 = Resistor [tolerance=±5% resistance=10 power=2W package="0805 [SMD]"]
  R35 = Resistor [tolerance=±5% resistance=100k package="0805 [SMD]"]
  R37 = Resistor [tolerance=±5% resistance=100k package="0805 [SMD]"]
  R23 = Resistor [tolerance=±5% resistance=1k package="0805 [SMD]"]
  R24 = Resistor [tolerance=±5% resistance=1k package="0805 [SMD]"]
  C11 = Ceramic Capacitor [capacitance=1µF package="0805 [SMD, multilayer]"]
  R38 = Resistor [tolerance=±5% resistance=100k package="0805 [SMD]"]
  R29 = Resistor [tolerance=±5% resistance=1k package="0805 [SMD]"]
  R30 = Resistor [tolerance=±5% resistance=1k package="0805 [SMD]"]
  R36 = Resistor [tolerance=±5% resistance=100k package="0805 [SMD]"]
  R9 = Resistor [tolerance=±5% resistance=100k package="0805 [SMD]"]
  R12 = Resistor [tolerance=±5% resistance=1k power=0.25W package="0805 [SMD]"]
  R10 = Resistor [tolerance=±5% resistance=100k power=0.25W package="0805 [SMD]"]
  R11 = Resistor [tolerance=±5% resistance=1k package="0805 [SMD]"]
  R13 = Resistor [tolerance=±5% resistance=100k package="0805 [SMD]"]
  R15 = Resistor [tolerance=±5% resistance=1k package="0805 [SMD]"]
  R14 = Resistor [tolerance=±5% resistance=100k package="0805 [SMD]"]
  R16 = Resistor [tolerance=±5% resistance=1k package="0805 [SMD]"]
  R41 = Resistor [tolerance=±5% resistance=470 package="0805 [SMD]"]
  C19 = Ceramic Capacitor [capacitance=0.01µF package="0805 [SMD, multilayer]"]
  R61 = Resistor [tolerance=±5% resistance=2.49k package="0805 [SMD]"]
  C15 = Ceramic Capacitor [capacitance=0.1µF voltage=50V package="0805 [SMD, multilayer]"]
  C13 = Ceramic Capacitor [capacitance=0.1µF voltage=50V package="0805 [SMD, multilayer]"]
  IC2 = IC, DIP package, 8 pins [chip_label=IC]
  C18 = Ceramic Capacitor [capacitance=10pF package="200 mil [THT, multilayer]"]
  C14 = Tantalum Capacitor [capacitance=47µF voltage=10V package="C 6032 [SMD, tantalum]"]
  C16 = Tantalum Capacitor [capacitance=10µF voltage=35V package="200 mil [THT, tantalum]"]
  D16 = Schottky Diode [part_number=1N5818 package="300 mil [THT]"]
  IC6 = ULN2003A [package="DIP16 [THT]"]
  IC4 = IC, DIP package, 8 pins [chip_label=SP720]
  HC-05 = Bluetooth HC-05 Macho
  IC5 = IC, DIP package, 8 pins [chip_label=SP720]
  R63 = Resistor [tolerance=±5% resistance=10k package="0805 [SMD]"]
  C26 = Ceramic Capacitor [capacitance=0.1µF package="0805 [SMD, multilayer]"]
  R64 = Resistor [tolerance=±5% resistance=470 package="0805 [SMD]"]
  C27 = Ceramic Capacitor [capacitance=0.22µF package="0805 [SMD, multilayer]"]
  C28 = Ceramic Capacitor [capacitance=0.1µF package="0805 [SMD, multilayer]"]
  R65 = Resistor [tolerance=±5% resistance=470 package="0805 [SMD]"]
  C29 = Ceramic Capacitor [capacitance=0.22µF package="0805 [SMD, multilayer]"]
  C23 = Ceramic Capacitor [capacitance=22µF package="0805 [SMD, multilayer]"]
  U4 = RS485 [package=so08]
  316370-6 = TE_Con_316370-6_040_II SRS_MK-II_48Pin_CAP-ASSY [part_number=316370-6 package="48-pin 0.040\" 3 row"]
  IC1 = SO08 [chip_label=IC package=SO]
  M1 = Mega2560 R3 Pro ch340g

nets:
  N1: Q1.gate, R11.Pin_1
  INJ-1-OUT: Q1.drain, 316370-6.2S, 316370-6.2V
  GND: Q1.source, Q2.source, Q3.source, Q4.source, U1.GND, U2.P$2, IC3.pin6, Q5.source, Q7.source, Q6.source, Q8.source, DRV8825.GND, C5.0, C20.0, C12.0, C4.0, C2.0, C1.0, C8.1, C7.0, C24.1, C10.0, C9.0, C25.0, C3.0, C6.0, R21.Pin_1, R49.Pin_0, R55.Pin_0, R48.Pin_0, R56.Pin_0, R35.Pin_0, R37.Pin_0, C11.0, R38.Pin_0, R36.Pin_0, R9.Pin_1, R10.Pin_1, R13.Pin_1, R14.Pin_1, C19.0, C15.0, C13.0, IC2.pin3, C18.1, C14.-, C16.-, D16.cathode, IC6.0V, IC4.pin4, HC-05.GND, IC5.pin4, C26.0, C27.0, C28.0, C29.0, C23.1, U4.DE, 316370-6.1K, 316370-6.1M, 316370-6.1T, 316370-6.1U, 316370-6.2I, 316370-6.2K, IC1.3
  N2: Q2.gate, R15.Pin_1
  INJ-3-OUT: Q2.drain, 316370-6.2Q, 316370-6.2R
  N3: Q3.gate, R12.Pin_1
  INJ-2-OUT: Q3.drain, 316370-6.2U, 316370-6.2X
  N4: Q4.gate, R16.Pin_1
  INJ-4-OUT: Q4.drain, 316370-6.2T, 316370-6.2W
  N5: U1.input_voltage, D15.cathode
  5V: U1.output_voltage, IC3.pin5, JP1.pin3, DRV8825.RESET, DRV8825.SLEEP, C20.1, R62.Pin_1, R1.Pin_0, R40.Pin_0, R39.Pin_0, R3.Pin_0, R54.Pin_1, C19.1, R61.Pin_1, C13.1, C14.+, D16.anode, IC4.pin8, HC-05.VCC, IC5.pin8, U4._RE, 316370-6.1V, 316370-6.1W, 316370-6.1X, M1.VTG, M1.5V
  12V/12V-raw: D15.anode, U2.P$1, JP1.pin1, R7.Pin_0, C15.1, C16.+, IC6.COM_-_Common, R63.Pin_1, 316370-6.2M
  VR1-: IC3.pin1, 316370-6.1R
  N6: IC3.pin2, JP2.pin3
  N7: IC3.pin3, JP3.pin1
  VR2-: IC3.pin4, 316370-6.1Q
  ADC Clamp7/TACH2-CPU-D18: IC3.pin7, R60.Pin_1, C24.0, M1.18
  ADC Clamp5/TACH1-CPU-D19: IC3.pin8, R59.Pin_1, C25.1, M1.19
  JP1-OUT: JP1.pin2, C12.1, C11.1, IC2.pin6, IC1.6
  N8: JP2.pin1, R59.Pin_0
  VR1+: JP2.pin2, JP4.pin2, 316370-6.1N
  VR2+: JP3.pin2, JP5.pin1, 316370-6.1O
  N9: JP3.pin3, R60.Pin_0
  N10: JP4.pin1, R39.Pin_1
  N11: JP5.pin2, R40.Pin_1
  N12: Q5.gate, R55.Pin_1, R57.Pin_1
  HC-1-OUT: Q5.drain, 316370-6.2N
  N13: Q7.gate, R48.Pin_1, R50.Pin_1
  IDLE-OUT: Q7.drain, 316370-6.2L
  N14: Q6.gate, R56.Pin_1, R58.Pin_1
  HC-2-OUT: Q6.drain, 316370-6.2J
  N15: Q8.gate, R49.Pin_1, R51.Pin_1
  BOOST-OUT: Q8.drain, 316370-6.2P
  CPU-D24: DRV8825.ENABLE, M1.24
  STEP-CPU-D17: DRV8825.STEP, M1.17
  STEPDIR-CPU-D16: DRV8825.DIR, M1.16
  STEP-1B-OUT: DRV8825.1B, 316370-6.2G
  STEP-1A-OUT: DRV8825.1A, 316370-6.2D
  STEP-2A-OUT: DRV8825.2A, 316370-6.2A
  STEP-2B-OUT: DRV8825.2B, 316370-6.2B
  N16: J142.pin1, R54.Pin_0
  RESET: J142.pin2, M1.RST
  N17: J142.pin3, R62.Pin_0, C23.0
  TPS Sensor: C5.1, R6.Pin_0, 316370-6.1G
  ADC Clamp2/CLT-CPU-A1: C4.1, R4.Pin_1, IC5.pin1, M1.A1
  ADC Clamp6/IAT-CPU-A0: C2.1, R2.Pin_1, IC5.pin7, M1.A0
  IAT Sensor: C1.1, R1.Pin_1, R2.Pin_0, 316370-6.1L
  N18: R7.Pin_1, C7.1, R8.Pin_0, R21.Pin_0
  ADC Clamp4/BRV-CPU-A4: C8.0, R8.Pin_1, M1.A4
  CLT Sensor: R3.Pin_1, C3.1, R4.Pin_0, 316370-6.1J
  ADC Clamp1/O2-CPU-A8: C10.1, R22.Pin_1, M1.A8
  O2 Sensor: C9.1, R22.Pin_0, 316370-6.1B
  ADC Clamp3/TPS-CPU-A2: R6.Pin_1, C6.1, M1.A2
  IGN-3-OUT: R31.Pin_0, 316370-6.2C
  N19: R31.Pin_1, IC2.pin7
  N20: R32.Pin_0, IC2.pin5
  IGN-4-OUT: R32.Pin_1, 316370-6.2F
  CPU-D7: R51.Pin_0, M1.7▀
  CPU-D6: R57.Pin_0, M1.6▀
  CPU-D5: R50.Pin_0, M1.5▀
  CPU-D4: R58.Pin_0, M1.4▀
  IGN-2-OUT: R27.Pin_0, 316370-6.2E
  N21: R27.Pin_1, IC1.7
  N22: R25.Pin_0, IC1.5
  IGN-1-OUT: R25.Pin_1, 316370-6.2H
  N23: R35.Pin_1, R24.Pin_1, IC1.4
  N24: R37.Pin_1, R23.Pin_1, IC1.2
  IGN2-CPU-D24: R23.Pin_0, M1.38
  IGN1-CPU-D28: R24.Pin_0, M1.40
  N25: R38.Pin_1, R29.Pin_1, IC2.pin2
  IGN3-CPU-D40: R29.Pin_0, M1.52/SCK
  IGN4-CPU-D36: R30.Pin_0, M1.50/MISO
  N26: R30.Pin_1, R36.Pin_1, IC2.pin4
  INJ1-CPU-D8: R9.Pin_0, R11.Pin_0, M1.8▀
  INJ2-CPU-D9: R12.Pin_0, R10.Pin_0, M1.9▀
  INJ3-CPU-D10: R13.Pin_0, R15.Pin_0, M1.10▀
  INJ4-CPU-D11: R14.Pin_0, R16.Pin_0, M1.11▀
  EXT-MAP: R41.Pin_0, U4.DI, 316370-6.1S
  ACD Clamp8/MAP-CPU-A3: R41.Pin_1, C18.0, IC4.pin7, 316370-6.1P, M1.A3
  ACD Clamp9/CPU-D2/Flex: R61.Pin_0, 316370-6.2O, M1.3▀
  RST-CPU-D48: IC6.In_2, M1.43
  LC-CPU-D47: IC6.In_3, M1.47
  LC-CPU-D45: IC6.In_4, M1.45
  LC-CPU-D49: IC6.In_5, M1.49
  LC-4-OUT: IC6.Out_5, R63.Pin_0, 316370-6.1I
  LC-3-OUT: IC6.Out_4, 316370-6.1F
  LC-2-OUT: IC6.Out_3, 316370-6.1C
  LC-1-OUT: IC6.Out_2, 316370-6.1E
  RX: HC-05.TXD, M1.RX0▼
  TX: HC-05.RXD, M1.TX1▲
  FuelPress: C26.1, R64.Pin_0, 316370-6.1D
  FuelPress-A5: R64.Pin_1, C27.1, M1.A5
  OilPress: C28.1, R65.Pin_0, 316370-6.1A
  OilPress-A7: R65.Pin_1, C29.1, M1.A7
  LC-5-OUT/LC-CPU-D51: 316370-6.1H, M1.51/MOSI
  SCL-CPU-D21: M1.21
  SDA-CPU-D20: M1.20

notes:
  Inlet Air Temperature sensor
  Coolant Temperature Sensor
  Speeduino v0.4, Throttle Position Sensor
  Battery Reference Voltage
  Injector 1
  Speeduino v0.4, Connector 1
  Injector 3
  Injector 2
  Injector 4
  Speeduino v0.4, O2 Sensor
  Ignitor output 1
  12v
  5v
  Power supply
  IGN Out
  Crank and Cam sensors
  Speeduino v0.4, MAP sensor input
  DetonationEMS.com
  Generic Outputs - High Current
  inj1
  VR
  Hall
  Reset Protection - Refer AVR040 Application note
  Stepper Driver
  PWM Idle / Boost
  Proto Area
  Run  Prog
  Aaron S. 2020
  Flex-Fuel  Input
  ULN2003a

custom parts:
  TE_Con_316370-6_040_II SRS_MK-II_48Pin_CAP-ASSY: TE Connectors_316370-6_040_II SRS_MK-II_48Pin_CAP-ASSY
  Mega2560 R3 Pro ch340g: The Mega 2560 R3 Pro Mini :- Completely compatible with original Arduino Mega2560 Pin pitch: 0.1 inch Size: 5.42cm*3.68cm With Atmega16U2 chip as the USB to Serial converter 5V working voltage. Input Voltage:7-12V Analog Input Pins: 16 Digital I/O pins: 54 The Mega 2560 R3 Pro Mini has no datasheet and no info and I don't have one to compare, so I made this based on photos. Dec 2019 modified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
