# Fritzing sketch v1.0.0.0.0 (saved by Fritzing 0.9.4)
circuit board: 10cm x 10cm

parts:
  Q1 = Basic FET N-Channel [part_number=STP62NS04Z package="TO220 [THT]"]
  Q2 = Basic FET N-Channel [part_number=STP62NS04Z package="TO220 [THT]"]
  Q3 = Basic FET N-Channel [part_number=STP62NS04Z package="TO220 [THT]"]
  Q4 = Basic FET N-Channel [part_number=STP62NS04Z package="TO220 [THT]"]
  U1 = Voltage Regulator - 5V [part_number=LM2940T-5.0 package="TO220 [THT]"]
  D15 = Schottky Diode [part_number=1N5818 package="300 mil [THT]"]
  U2 = V18ZA2P [part_number=ERZV14D220 package=v18za2p]
  IC3 = IC, DIP package, 8 pins [chip_label="Dual VR Conditioner"]
  JP1 = female pin header, 3 pins [form="♀ (female)"]
  JP2 = female pin header, 3 pins [form="♀ (female)"]
  JP3 = female pin header, 3 pins [form="♀ (female)"]
  JP4 = female pin header, 2 pins [form="♀ (female)"]
  JP5 = female pin header, 2 pins [form="♀ (female)"]
  D17 = Schottky Diode [part_number=1N5818 package="300 mil [THT]"]
  Q5 = Basic FET N-Channel [part_number=STP62NS04Z package="TO220 [THT]"]
  Q7 = Basic FET N-Channel [part_number=STP62NS04Z package="TO220 [THT]"]
  Q6 = Basic FET N-Channel [part_number=STP62NS04Z package="TO220 [THT]"]
  J4 = shrouded pin header, 40 pins [form="♂ (shrouded male)"]
  Q8 = Basic FET N-Channel [part_number=STP62NS04Z package="TO220 [THT]"]
  J45 = female pin header, 1 pin [form="♀ (female)"]  # not connected
  J46 = female pin header, 1 pin [form="♀ (female)"]  # not connected
  J49 = female pin header, 1 pin [form="♀ (female)"]  # not connected
  J57 = female pin header, 1 pin [form="♀ (female)"]
  J58 = female pin header, 1 pin [form="♀ (female)"]
  J60 = female pin header, 1 pin [form="♀ (female)"]
  J62 = female pin header, 1 pin [form="♀ (female)"]
  J68 = female pin header, 1 pin [form="♀ (female)"]
  DRV8825 = Pololu A4988 [package=SO16]
  J71 = female pin header, 1 pin [form="♀ (female)"]  # not connected
  J72 = female pin header, 1 pin [form="♀ (female)"]  # not connected
  J73 = female pin header, 1 pin [form="♀ (female)"]  # not connected
  J74 = female pin header, 1 pin [form="♀ (female)"]  # not connected
  J78 = female pin header, 1 pin [form="♀ (female)"]  # not connected
  J80 = female pin header, 1 pin [form="♀ (female)"]  # not connected
  J81 = female pin header, 1 pin [form="♀ (female)"]  # not connected
  J82 = female pin header, 1 pin [form="♀ (female)"]  # not connected
  J83 = female pin header, 1 pin [form="♀ (female)"]  # not connected
  J84 = female pin header, 1 pin [form="♀ (female)"]  # not connected
  J85 = female pin header, 1 pin [form="♀ (female)"]  # not connected
  J86 = female pin header, 1 pin [form="♀ (female)"]  # not connected
  J87 = female pin header, 1 pin [form="♀ (female)"]  # not connected
  J90 = female pin header, 1 pin [form="♀ (female)"]  # not connected
  J92 = female pin header, 1 pin [form="♀ (female)"]  # not connected
  J93 = female pin header, 1 pin [form="♀ (female)"]  # not connected
  J94 = female pin header, 1 pin [form="♀ (female)"]  # not connected
  J95 = female pin header, 1 pin [form="♀ (female)"]  # not connected
  J96 = female pin header, 1 pin [form="♀ (female)"]  # not connected
  J111 = female pin header, 1 pin [form="♀ (female)"]  # not connected
  J113 = female pin header, 1 pin [form="♀ (female)"]  # not connected
  J114 = female pin header, 1 pin [form="♀ (female)"]
  J119 = female pin header, 1 pin [form="♀ (female)"]  # not connected
  J123 = female pin header, 1 pin [form="♀ (female)"]  # not connected
  J142 = female pin header, 3 pins [form="♀ (female)"]
  J143 = female pin header, 1 pin [form="♀ (female)"]  # not connected
  J144 = female pin header, 1 pin [form="♀ (female)"]  # not connected
  J3 = screw terminal, 2 pins
  MPX4250AP1 = MPX4250AP pressure sensor [part_number=MPX]
  C5 = Ceramic Capacitor [capacitance=0.1µF package="0805 [SMD, multilayer]"]
  C20 = Ceramic Capacitor [capacitance=1µF package="0805 [SMD, multilayer]"]
  LED3 = smd LED [color="Red (633nm)" package="0805 [SMD]"]
  LED4 = smd LED [color="Red (633nm)" package="0805 [SMD]"]
  C12 = Ceramic Capacitor [capacitance=1µF package="0805 [SMD, multilayer]"]
  C4 = Ceramic Capacitor [capacitance=0.22µF package="0805 [SMD, multilayer]"]
  R62 = Resistor [tolerance=±5% resistance=120 package="0805 [SMD]"]
  C2 = Ceramic Capacitor [capacitance=0.22µF package="0805 [SMD, multilayer]"]
  C1 = Ceramic Capacitor [capacitance=0.1µF package="0805 [SMD, multilayer]"]
  C23 = Ceramic Capacitor [capacitance=4.7nF package="0603 [SMD, multilayer]"]
  R7 = Resistor [tolerance=±0.1% resistance=3.9k package="0805 [SMD]"]
  R1 = Resistor [tolerance=±0.1% resistance=2.49k package="0805 [SMD]"]
  C8 = Ceramic Capacitor [capacitance=0.22µF package="0805 [SMD, multilayer]"]
  C7 = Ceramic Capacitor [capacitance=0.1µF package="0805 [SMD, multilayer]"]
  R59 = Resistor [tolerance=±5% resistance=1k package="0805 [SMD]"]
  R40 = Resistor [tolerance=±5% resistance=1k package="0805 [SMD]"]
  R39 = Resistor [tolerance=±5% resistance=1k package="0805 [SMD]"]
  R60 = Resistor [tolerance=±5% resistance=1k package="0805 [SMD]"]
  C24 = Ceramic Capacitor [capacitance=0.22µF package="0805 [SMD, multilayer]"]
  R3 = Resistor [tolerance=±0.1% resistance=2.49k package="0805 [SMD]"]
  C10 = Ceramic Capacitor [capacitance=0.22µF package="0805 [SMD, multilayer]"]
  C9 = Ceramic Capacitor [capacitance=0.1µF package="0805 [SMD, multilayer]"]
  C25 = Ceramic Capacitor [capacitance=0.01µF package="0805 [SMD, multilayer]"]
  C3 = Ceramic Capacitor [capacitance=0.1µF package="0805 [SMD, multilayer]"]
  R2 = Resistor [tolerance=±5% resistance=470 package="0805 [SMD]"]
  R4 = Resistor [tolerance=±5% resistance=470 package="0805 [SMD]"]
  R54 = Resistor [tolerance=±5% resistance=470 package="0805 [SMD]"]
  R22 = Resistor [tolerance=±5% resistance=470 package="0805 [SMD]"]
  R6 = Resistor [tolerance=±5% resistance=470 package="0805 [SMD]"]
  C6 = Ceramic Capacitor [capacitance=0.22µF package="0805 [SMD, multilayer]"]
  R33 = Resistor [tolerance=±5% resistance=2.4k power=0.25W package="0805 [SMD]"]
  R31 = Resistor [tolerance=±5% resistance=10 power=1 package="0805 [SMD]"]
  R34 = Resistor [tolerance=±5% resistance=2.4k package="0805 [SMD]"]
  R32 = Resistor [tolerance=±5% resistance=10 power=2W package="0805 [SMD]"]
  R8 = Resistor [tolerance=±5% resistance=470 package="0805 [SMD]"]
  R21 = Resistor [tolerance=±5% resistance=1k package="0805 [SMD]"]
  IC4 = SSOP16 [chip_label=SP720 package=SSOP]
  R49 = Resistor [tolerance=±5% resistance=100k power=0.25W package="0805 [SMD]"]
  R55 = Resistor [tolerance=±5% resistance=100k package="0805 [SMD]"]
  R48 = Resistor [tolerance=±5% resistance=100k package="0805 [SMD]"]
  R56 = Resistor [tolerance=±5% resistance=100k power=0.25W package="0805 [SMD]"]
  R51 = Resistor [tolerance=±5% resistance=1k package="0805 [SMD]"]
  R57 = Resistor [tolerance=±5% resistance=1k package="0805 [SMD]"]
  R50 = Resistor [tolerance=±5% resistance=1k package="0805 [SMD]"]
  R58 = Resistor [tolerance=±5% resistance=1k package="0805 [SMD]"]
  LED2 = smd LED [color="Red (633nm)" package="0805 [SMD]"]
  LED1 = smd LED [color="Red (633nm)" package="0805 [SMD]"]
  R28 = Resistor [tolerance=±5% resistance=2.4k package="0805 [SMD]"]
  R26 = Resistor [tolerance=±5% resistance=2.4k package="0805 [SMD]"]
  R27 = Resistor [tolerance=±5% resistance=160 power=2W package="0805 [SMD]"]
  R25 = Resistor [tolerance=±5% resistance=10 power=2W package="0805 [SMD]"]
  IC1 = SO08 [chip_label=IC package=SO]
  R35 = Resistor [tolerance=±5% resistance=100k package="0805 [SMD]"]
  R37 = Resistor [tolerance=±5% resistance=100k package="0805 [SMD]"]
  R23 = Resistor [tolerance=±5% resistance=1k package="0805 [SMD]"]
  R24 = Resistor [tolerance=±5% resistance=1k package="0805 [SMD]"]
  C11 = Ceramic Capacitor [capacitance=1µF package="0805 [SMD, multilayer]"]
  R38 = Resistor [tolerance=±5% resistance=100k package="0805 [SMD]"]
  R29 = Resistor [tolerance=±5% resistance=1k package="0805 [SMD]"]
  R30 = Resistor [tolerance=±5% resistance=1k package="0805 [SMD]"]
  R36 = Resistor [tolerance=±5% resistance=100k package="0805 [SMD]"]
  IC2 = SO08 [chip_label=IC package=SO]
  R9 = Resistor [tolerance=±5% resistance=100k package="0805 [SMD]"]
  R12 = Resistor [tolerance=±5% resistance=1k power=0.25W package="0805 [SMD]"]
  R10 = Resistor [tolerance=±5% resistance=100k power=0.25W package="0805 [SMD]"]
  R11 = Resistor [tolerance=±5% resistance=1k package="0805 [SMD]"]
  R13 = Resistor [tolerance=±5% resistance=100k package="0805 [SMD]"]
  R15 = Resistor [tolerance=±5% resistance=1k package="0805 [SMD]"]
  R14 = Resistor [tolerance=±5% resistance=100k package="0805 [SMD]"]
  R16 = Resistor [tolerance=±5% resistance=1k package="0805 [SMD]"]
  R41 = Resistor [tolerance=±5% resistance=470 package="0805 [SMD]"]
  C19 = Ceramic Capacitor [capacitance=0.01µF package="0805 [SMD, multilayer]"]
  C18 = Ceramic Capacitor [capacitance=0.3µF package="0805 [SMD, multilayer]"]
  12v_Jump = ULN2003A [package="SO16 [SMD]"]
  R61 = Resistor [tolerance=±5% resistance=2.49k package="0805 [SMD]"]
  D16 = Diode [package=smb-diode]
  C15 = Ceramic Capacitor [capacitance=0.1µF voltage=50V package="0805 [SMD, multilayer]"]
  C13 = Ceramic Capacitor [capacitance=0.1µF voltage=50V package="0805 [SMD, multilayer]"]
  C14 = Tantalum Capacitor [capacitance=47µF voltage=10V package="D 7343 [SMD, tantalum]"]
  C16 = Tantalum Capacitor [capacitance=10µF voltage=35V package="B 3528 [SMD, tantalum]"]
  R63 = Resistor [tolerance=±5% resistance=10k package=THT]
  M1 = Mega2560 R3 Pro ch340g

nets:
  N1: Q1.gate, R11.Pin_1
  INJ-1-OUT: Q1.drain, J4.pin1, J4.pin40
  GND: Q1.source, Q2.source, Q3.source, Q4.source, U1.GND, U2.P$2, IC3.pin6, Q5.source, Q7.source, Q6.source, J4.pin9, J4.pin10, J4.pin12, J4.pin23, Q8.source, DRV8825.GND, J3.pin1, MPX4250AP1.GND, C5.0, C20.0, LED3.cathode, LED4.cathode, C12.0, C4.0, C2.0, C1.0, C23.0, C8.1, C7.0, C24.1, C10.0, C9.0, C25.1, C3.0, C6.0, R21.Pin_1, IC4.8, R49.Pin_0, R55.Pin_0, R48.Pin_0, R56.Pin_0, LED2.cathode, LED1.cathode, IC1.3, R35.Pin_0, R37.Pin_0, C11.0, R38.Pin_0, R36.Pin_0, IC2.3, R9.Pin_1, R10.Pin_1, R13.Pin_1, R14.Pin_1, C19.0, C18.1, 12v_Jump.0V, D16.A, C15.0, C13.0, C14.-, C16.-
  N2: Q2.gate, R15.Pin_1
  INJ-3-OUT: Q2.drain, J4.pin3, J4.pin4
  N3: Q3.gate, R12.Pin_1
  INJ-2-OUT: Q3.drain, J4.pin2, J4.pin39
  N4: Q4.gate, R16.Pin_1
  INJ-4-OUT: Q4.drain, J4.pin5, J4.pin6
  N5: U1.input_voltage, D15.cathode
  5V: U1.output_voltage, IC3.pin5, JP1.pin1, D17.cathode, J4.pin13, J4.pin28, DRV8825.RESET, DRV8825.SLEEP, MPX4250AP1.Vs, C20.1, R62.Pin_1, R1.Pin_0, R40.Pin_0, R39.Pin_0, R3.Pin_0, R54.Pin_1, IC4.16, C19.1, R61.Pin_1, D16.C, C13.1, C14.+, M1.VTG, M1.5V
  12V/12V-raw: D15.anode, U2.P$1, JP1.pin3, DRV8825.VMOT, J3.pin2, R7.Pin_0, 12v_Jump.COM_-_Common, C15.1, C16.+, R63.Pin_1
  VR1-: IC3.pin1, J4.pin27
  N6: IC3.pin2, JP2.pin3
  N7: IC3.pin3, JP3.pin1
  VR2-: IC3.pin4, J4.pin26
  ADC Clamp7/TACH2-CPU-D18: IC3.pin7, JP3.pin3, C24.0, IC4.6, M1.18
  ADC Clamp5/TACH1-CPU-D19: IC3.pin8, JP2.pin1, C25.0, IC4.5, M1.19
  JP1-OUT: JP1.pin2, C12.1, IC1.6, C11.1, IC2.6
  N8: JP2.pin2, R59.Pin_1
  N9: JP3.pin2, R60.Pin_1
  N10: JP4.pin1, R39.Pin_1
  VR1+: JP4.pin2, J4.pin25, R59.Pin_0
  VR2+: JP5.pin1, J4.pin24, R60.Pin_0
  N11: JP5.pin2, R40.Pin_1
  RESET: D17.anode, J142.pin2, C23.1, M1.RST
  N12: Q5.gate, R55.Pin_1, R57.Pin_1
  HC-1-OUT: Q5.drain, J4.pin36
  N13: Q7.gate, R48.Pin_1, R50.Pin_1
  IDLE-OUT: Q7.drain, J4.pin37
  N14: Q6.gate, R56.Pin_1, R58.Pin_1
  HC-2-OUT: Q6.drain, J4.pin38
  IGN-1-OUT: J4.pin7, R28.Pin_1, R27.Pin_0
  IGN-4-OUT: J4.pin8, R34.Pin_1, R32.Pin_1
  MAP-CPU-A3: J4.pin11, R41.Pin_1, C18.0, M1.A3
  LC-1-OUT: J4.pin14, 12v_Jump.Out_2
  LC-2-OUT: J4.pin15, 12v_Jump.Out_3
  LC-3-OUT: J4.pin16, 12v_Jump.Out_4
  LC-4-OUT: J4.pin17, 12v_Jump.Out_5, R63.Pin_0
  LC-5-OUT/LC-CPU-D51: J4.pin18, J57.pin1, M1.51/MOSI
  CLT Sensor: J4.pin19, R3.Pin_1, C3.1, R4.Pin_0
  IAT Sensor: J4.pin20, C1.1, R1.Pin_1, R2.Pin_0
  O2 Sensor: J4.pin21, C9.1, R22.Pin_0
  TPS Sensor: J4.pin22, C5.1, R6.Pin_0
  STEP-2B-OUT: J4.pin29, DRV8825.2B
  STEP-2A-OUT: J4.pin30, DRV8825.2A
  STEP-1A-OUT: J4.pin31, DRV8825.1A
  STEP-1B-OUT: J4.pin32, DRV8825.1B
  IGN-3-OUT: J4.pin33, R33.Pin_1, R31.Pin_0
  IGN-2-OUT: J4.pin34, R26.Pin_1, R25.Pin_1
  BOOST-OUT: J4.pin35, Q8.drain
  N15: Q8.gate, R49.Pin_1, R51.Pin_1
  LC-CPU-D49: J58.pin1, 12v_Jump.In_5, M1.49
  RST-CPU-D48: J60.pin1, 12v_Jump.In_2, M1.43
  LC-CPU-D45: J62.pin1, 12v_Jump.In_4, M1.45
  LC-CPU-D47: J68.pin1, 12v_Jump.In_3, M1.47
  CPU-D24: DRV8825.ENABLE, M1.24
  STEP-CPU-D17: DRV8825.STEP, M1.17
  STEPDIR-CPU-D16: DRV8825.DIR, M1.16
  CPU-D2: J114.pin1, R61.Pin_0, M1.3▀
  N16: J142.pin1, R54.Pin_0
  N17: J142.pin3, R62.Pin_0
  N18: MPX4250AP1.V_out, R41.Pin_0
  N19: LED3.anode, R34.Pin_0
  N20: LED4.anode, R33.Pin_0
  ADC Clamp2/CLT-CPU-A1: C4.1, R4.Pin_1, IC4.2, M1.A1
  ADC Clamp6/IAT-CPU-A0: C2.1, R2.Pin_1, IC4.1, M1.A0
  N21: R7.Pin_1, C7.1, R8.Pin_0, R21.Pin_0
  ADC Clamp4/BRV-CPU-A4: C8.0, R8.Pin_1, IC4.4, M1.A4
  ADC Clamp1/O2-CPU-A8: C10.1, R22.Pin_1, IC4.7, M1.A8
  ADC Clamp3/TPS-CPU-A2: R6.Pin_1, C6.1, IC4.3, M1.A2
  N22: R31.Pin_1, IC2.7
  N23: R32.Pin_0, IC2.5
  CPU-D7: R51.Pin_0, M1.7▀
  CPU-D6: R57.Pin_0, M1.6▀
  CPU-D5: R50.Pin_0, M1.5▀
  CPU-D4: R58.Pin_0, M1.4▀
  N24: LED2.anode, R28.Pin_0
  N25: LED1.anode, R26.Pin_0
  N26: R27.Pin_1, IC1.7
  N27: R25.Pin_0, IC1.5
  N28: IC1.2, R37.Pin_1, R23.Pin_1
  N29: IC1.4, R35.Pin_1, R24.Pin_1
  IGN1-CPU-D28: R23.Pin_0, M1.40
  IGN2-CPU-D24: R24.Pin_0, M1.38
  N30: R38.Pin_1, R29.Pin_1, IC2.2
  IGN3-CPU-D40: R29.Pin_0, M1.52/SCK
  IGN4-CPU-D36: R30.Pin_0, M1.50/MISO
  N31: R30.Pin_1, R36.Pin_1, IC2.4
  INJ1-CPU-D8: R9.Pin_0, R11.Pin_0, M1.8▀
  INJ2-CPU-D9: R12.Pin_0, R10.Pin_0, M1.9▀
  INJ3-CPU-D10: R13.Pin_0, R15.Pin_0, M1.10▀
  INJ4-CPU-D11: R14.Pin_0, R16.Pin_0, M1.11▀
  SCL-CPU-D21: M1.21
  SDA-CPU-D20: M1.20

notes:
  Inlet Air Temperature sensor
  Coolant Temperature Sensor
  Speeduino v0.4, Throttle Position Sensor
  Battery Reference Voltage
  Injector 1
  Speeduino v0.4, Connector 1
  Injector 3
  Injector 2
  Injector 4
  Speeduino v0.4, O2 Sensor
  Ignitor output 1
  Ignitor output 2
  12v
  5v
  Power supply
  IGN Out
  Crank and Cam sensors
  Speeduino v0.4, MAP sensor input
  DetonationEMS.com
  Generic Outputs - High Current
  inj1
  VR
  Hall
  Reset Protection - Refer AVR040 Application note
  Stepper Driver
  PWM Idle / Boost
  GND
  51
  49
  45
  47
  43
  Proto Area
  Flat side down
  ULN2003a
  Eth
  5v   |
  |   GND  |
  Run  Prog
  D12 D13
  v1.1b
  Aaron S. 2020

custom parts:
  Mega2560 R3 Pro ch340g: The Mega 2560 R3 Pro Mini :- Completely compatible with original Arduino Mega2560 Pin pitch: 0.1 inch Size: 5.42cm*3.68cm With Atmega16U2 chip as the USB to Serial converter 5V working voltage. Input Voltage:7-12V Analog Input Pins: 16 Digital I/O pins: 54 The Mega 2560 R3 Pro Mini has no datasheet and no info and I don't have one to compare, so I made this based on photos. Dec 2019 modified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
