# Fritzing sketch Breakout v3 (saved by Fritzing 0.9.4)
circuit board: 3cm x 7.5cm
breadboards: 1

parts:
  J4 = shrouded pin header, 40 pins [form="♂ (shrouded male)"]
  st2 = screw terminal, 14 pins
  st1 = screw terminal, 16 pins
  st3 = screw terminal, 8 pins

nets:
  INJ-1-OUT: J4.pin1, J4.pin40, st2.pin14
  INJ-2-OUT: J4.pin2, J4.pin39, st2.pin13
  INJ-3-OUT: J4.pin3, J4.pin4, st2.pin12
  INJ-4-OUT: J4.pin5, J4.pin6, st2.pin11
  IGN-1-OUT: J4.pin7, st2.pin10
  IGN-4-OUT: J4.pin8, st2.pin9
  GND: J4.pin9, J4.pin10, J4.pin12, J4.pin23, st3.pin3, st3.pin4, st3.pin5, st3.pin6, st3.pin7, st3.pin8
  MAP-CPU-A3: J4.pin11, st2.pin8
  5V: J4.pin13, J4.pin28, st3.pin1, st3.pin2
  LC-1-OUT: J4.pin14, st2.pin7
  LC-2-OUT: J4.pin15, st2.pin6
  LC-3-OUT: J4.pin16, st2.pin5
  LC-4-OUT: J4.pin17, st2.pin4
  LC-5-OUT: J4.pin18, st2.pin3
  CLT Sensor: J4.pin19, st2.pin2
  IAT Sensor: J4.pin20, st2.pin1
  O2 Sensor: J4.pin21, st1.pin16
  TPS Sensor: J4.pin22, st1.pin15
  VR2+: J4.pin24, st1.pin14
  VR1+: J4.pin25, st1.pin13
  VR2-: J4.pin26, st1.pin12
  VR1-: J4.pin27, st1.pin11
  STEP-2B-OUT: J4.pin29, st1.pin10
  STEP-2A-OUT: J4.pin30, st1.pin9
  STEP-1A-OUT: J4.pin31, st1.pin8
  STEP-1B-OUT: J4.pin32, st1.pin7
  IGN-3-OUT: J4.pin33, st1.pin6
  IGN-2-OUT: J4.pin34, st1.pin5
  BOOST-OUT: J4.pin35, st1.pin4
  HC-1-OUT: J4.pin36, st1.pin3
  IDLE-OUT: J4.pin37, st1.pin2
  HC-2-OUT: J4.pin38, st1.pin1

notes:
  Screw Terminal, IDC 40
  inj1
  Aaron S. (Detonation)
  <-
  24
  GND GND GND GND GND GND
  5V 5V
  o2 TPS
  DetonationEMS.com
  ID2B ID2A ID1A ID1B
  VR2+ VR1+ VR2- VR1-
  IGN3 IGN2
  INJ1 INJ2 INJ3 INJ4
  IGN1 IGN4 MAP
  BOOST ID2 PWM VVT
  FAN   FP  TACH CLUTCH
  CLT IAT
  Aaron S. 2020
  Screw Terminal, Screw Terminal
  PIN43
