# Fritzing sketch Breakout v4 (saved by Fritzing 0.9.4)
circuit board: 5.5cm x 2cm
breadboards: 1

parts:
  st1 = screw terminal, 20 pins
  st2 = screw terminal, 20 pins
  J4 = shrouded pin header, 40 pins [form="♂ (shrouded male)"]

nets:
  INJ-1-OUT: st1.pin1, st2.pin1, J4.pin1, J4.pin40
  INJ-2-OUT: st1.pin2, st2.pin2, J4.pin2, J4.pin39
  HC-2-OUT: st1.pin3, J4.pin38
  IDLE-OUT: st1.pin4, J4.pin37
  HC-1-OUT: st1.pin5, J4.pin36
  BOOST-OUT: st1.pin6, J4.pin35
  IGN-2-OUT: st1.pin7, J4.pin34
  IGN-3-OUT: st1.pin8, J4.pin33
  STEP-1B-OUT: st1.pin9, J4.pin32
  STEP-1A-OUT: st1.pin10, J4.pin31
  STEP-2A-OUT: st1.pin11, J4.pin30
  STEP-2B-OUT: st1.pin12, J4.pin29
  5V: st1.pin13, st2.pin13, J4.pin13, J4.pin28
  VR1-: st1.pin14, J4.pin27
  VR2-: st1.pin15, J4.pin26
  VR1+: st1.pin16, J4.pin25
  VR2+: st1.pin17, J4.pin24
  TPS Sensor: st1.pin19, J4.pin22
  O2 Sensor: st1.pin20, J4.pin21
  INJ-3-OUT: st2.pin3, st2.pin4, J4.pin3, J4.pin4
  INJ-4-OUT: st2.pin5, st2.pin6, J4.pin5, J4.pin6
  IGN-1-OUT: st2.pin7, J4.pin7
  IGN-4-OUT: st2.pin8, J4.pin8
  MAP-CPU-A3: st2.pin11, J4.pin11
  LC-1-OUT: st2.pin14, J4.pin14
  LC-2-OUT: st2.pin15, J4.pin15
  LC-3-OUT: st2.pin16, J4.pin16
  LC-4-OUT: st2.pin17, J4.pin17
  LC-5-OUT: st2.pin18, J4.pin18
  CLT Sensor: st2.pin19, J4.pin19
  IAT Sensor: st2.pin20, J4.pin20
  GND: J4.pin9, J4.pin10, J4.pin12, J4.pin23

notes:
  Screw Terminal, IDC 40
  inj1
  Aaron S. (Detonation)
  <-
  24
  DetonationEMS.com
  Aaron S. 2020
  Screw Terminal, Screw Terminal
