# Fritzing sketch VR Conditioner v0.0.0.1 (saved by Fritzing 0.9.4)
circuit board: 3.62168cm x 4.3936cm
breadboards: 1

parts:
  IC1 = IC, DIP package, 8 pins [chip_label=IC]
  R10 = Resistor [tolerance=±5% resistance=4.7k power=3W package=THT]
  R12 = Resistor [tolerance=±5% resistance=4.7k power=3W package=THT]
  R6 = Resistor [tolerance=±1% resistance=1k package="0805 [SMD]"]
  R4 = Resistor [tolerance=±1% resistance=1k package="0805 [SMD]"]
  R9 = Resistor [tolerance=±5% resistance=10k package="0805 [SMD]"]
  R7 = Resistor [tolerance=±5% resistance=10k package="0805 [SMD]"]
  C4 = Ceramic Capacitor [capacitance=1nF package="0805 [SMD, multilayer]"]
  R13 = Resistor [tolerance=±5% resistance=10k package="0805 [SMD]"]
  C5 = Ceramic Capacitor [capacitance=1nF package="0805 [SMD, multilayer]"]
  R11 = Resistor [tolerance=±5% resistance=10k package="0805 [SMD]"]
  J1 = female pin header, 2 pins [form="♀ (female)"]
  LM1815 = IC, DIP package, 14 pins [chip_label=LM1815N]
  C2_0_001uf = Ceramic Capacitor [capacitance=0.01µF voltage=6.3V package="200 mil [THT, multilayer]"]
  R14 = Resistor [tolerance=±5% resistance=150k package=THT]

nets:
  VR1-: IC1.pin1, R10.Pin_1, R9.Pin_1
  VR1+: IC1.pin2, R10.Pin_0, R7.Pin_1
  VR2+: IC1.pin3, R12.Pin_0, R13.Pin_1
  VR2-: IC1.pin4, R12.Pin_1, R11.Pin_1
  5V: IC1.pin5, R6.Pin_0, R4.Pin_0, R14.Pin_1
  GND: IC1.pin6, LM1815.pin2, C2_0_001uf.0
  Output2: IC1.pin7, R6.Pin_1, J1.pin1
  Output1: IC1.pin8, R4.Pin_1, J1.pin2
  N1: R9.Pin_0, C4.0
  N2: R7.Pin_0, C4.1
  N3: R13.Pin_0, C5.1
  N4: C5.0, R11.Pin_0
  N5: LM1815.pin14, C2_0_001uf.1, R14.Pin_0

notes:
  I/O Connector
  VR Conditioner - Operating mode A2
  Bottom
  Top
  Dual VR Conditioner v3.1
  © Josh Stewart
  5v
  GND
  Out2
  Out1
