# Fritzing sketch v1.0.0.7 (saved by Fritzing 0.9.4)
circuit board: 10cm x 10cm
breadboards: 1

parts:
  Arduino_Mega_2560 = Arduino Mega 2560 (Rev3) [part_number="Arduino Mega 2560"]
  R1 = Resistor [tolerance=±0.1% resistance=2.49k part_number=RC55Y-2K49BI package=THT]
  R2 = Resistor [tolerance=±5% resistance=470 package=THT]
  R3 = Resistor [tolerance=±0.1% resistance=2.49k part_number=RC55Y-2K49BI package=THT]
  R4 = Resistor [tolerance=±5% resistance=470 package=THT]
  R6 = Resistor [tolerance=±5% resistance=470 package=THT]
  R7 = Resistor [tolerance=±0.1% resistance=3.9k package=THT]
  R8 = Resistor [tolerance=±5% resistance=470 package=THT]
  Q1 = Basic FET N-Channel [part_number=STP62NS04Z package="TO220 [THT]"]
  R10 = Resistor [tolerance=±5% resistance=1k package=THT]
  R11 = Resistor [tolerance=±5% resistance=100k package=THT]
  C7 = Ceramic Capacitor [capacitance=0.1µF package="200 mil [THT, multilayer]"]
  C1 = Ceramic Capacitor [capacitance=0.1µF package="200 mil [THT, multilayer]"]
  C3 = Ceramic Capacitor [capacitance=0.1µF package="200 mil [THT, multilayer]"]
  C5 = Ceramic Capacitor [capacitance=0.1µF package="200 mil [THT, multilayer]"]
  J3 = screw terminal, 2 pins
  Q2 = Basic FET N-Channel [part_number=STP62NS04Z package="TO220 [THT]"]
  R16 = Resistor [tolerance=±5% resistance=1k package=THT]
  R17 = Resistor [tolerance=±5% resistance=100k package=THT]
  Q3 = Basic FET N-Channel [part_number=STP62NS04Z package="TO220 [THT]"]
  R13 = Resistor [tolerance=±5% resistance=1k power=0.25W package=THT]
  R14 = Resistor [tolerance=±5% resistance=100k power=0.25W package=THT]
  Q4 = Basic FET N-Channel [part_number=STP62NS04Z package="TO220 [THT]"]
  R19 = Resistor [tolerance=±5% resistance=1k package=THT]
  R20 = Resistor [tolerance=±5% resistance=100k package=THT]
  C2 = Ceramic Capacitor [capacitance=0.22µF package="200 mil [THT, multilayer]"]
  C8 = Ceramic Capacitor [capacitance=0.22µF package="200 mil [THT, multilayer]"]
  R21 = Resistor [tolerance=±5% resistance=1k package=THT]
  C9 = Ceramic Capacitor [capacitance=0.1µF package="200 mil [THT, multilayer]"]
  R22 = Resistor [tolerance=±5% resistance=470 package=THT]
  C6 = Ceramic Capacitor [capacitance=0.22µF package="200 mil [THT, multilayer]"]
  C4 = Ceramic Capacitor [capacitance=0.22µF package="200 mil [THT, multilayer]"]
  C10 = Ceramic Capacitor [capacitance=0.22µF package="200 mil [THT, multilayer]"]
  IC1 = IC, DIP package, 8 pins [chip_label=IC part_number=TC4424EPA]
  R23 = Resistor [tolerance=±5% resistance=1k package=THT]
  R24 = Resistor [tolerance=±5% resistance=1k package=THT]
  C11 = Ceramic Capacitor [capacitance=1µF package="200 mil [THT, multilayer]"]
  R25 = Resistor [tolerance=±5% resistance=160 power=2W package=THT]
  R26 = Resistor [tolerance=±5% resistance=2.4k package=THT]
  R27 = Resistor [tolerance=±5% resistance=160 power=2W package=THT]
  R28 = Resistor [tolerance=±5% resistance=2.4k package=THT]
  IC2 = IC, DIP package, 8 pins [chip_label=IC part_number=TC4424EPA]
  R29 = Resistor [tolerance=±5% resistance=1k package=THT]
  R30 = Resistor [tolerance=±5% resistance=1k package=THT]
  C12 = Ceramic Capacitor [capacitance=1µF package="200 mil [THT, multilayer]"]
  R31 = Resistor [tolerance=±5% resistance=160 power=2W package=THT]
  R33 = Resistor [tolerance=±5% resistance=2.4k power=0.25W package=THT]
  R34 = Resistor [tolerance=±5% resistance=2.4k package=THT]
  U1 = Voltage Regulator - 5V [part_number=LM2940T-5.0 package="TO220 [THT]"]
  D15 = Schottky Diode [part_number=1N5818 package="300 mil [THT]"]
  C14 = Tantalum Capacitor [capacitance=47µF voltage=10V package="200 mil [THT, tantalum]"]
  C13 = Ceramic Capacitor [capacitance=0.1µF voltage=50V package="200 mil [THT, multilayer]"]
  C15 = Ceramic Capacitor [capacitance=0.1µF voltage=50V package="200 mil [THT, multilayer]"]
  C16 = Tantalum Capacitor [capacitance=10µF voltage=35V package="200 mil [THT, tantalum]"]
  U2 = V18ZA2P [part_number=ERZV14D220 package=v18za2p]
  R35 = Resistor [tolerance=±5% resistance=100k package=THT]
  R36 = Resistor [tolerance=±5% resistance=100k package=THT]
  R37 = Resistor [tolerance=±5% resistance=100k package=THT]
  R38 = Resistor [tolerance=±5% resistance=100k package=THT]
  IC3 = IC, DIP package, 8 pins [chip_label="Dual VR Conditioner"]
  JP1 = female pin header, 3 pins [form="♀ (female)"]
  JP2 = female pin header, 3 pins [form="♀ (female)"]
  JP3 = female pin header, 3 pins [form="♀ (female)"]
  R39 = Resistor [tolerance=±5% resistance=1k package=THT]
  JP4 = female pin header, 2 pins [form="♀ (female)"]
  R40 = Resistor [tolerance=±5% resistance=1k package=THT]
  JP5 = female pin header, 2 pins [form="♀ (female)"]
  C18 = Ceramic Capacitor [capacitance=0.3µF package="200 mil [THT, multilayer]"]
  R41 = Resistor [tolerance=±5% resistance=470 package=THT]
  C19 = Ceramic Capacitor [capacitance=0.01µF package="200 mil [THT, multilayer]"]
  C20 = Ceramic Capacitor [capacitance=1µF package="200 mil [THT, multilayer]"]
  R48 = Resistor [tolerance=±5% resistance=100k package=THT]
  R49 = Resistor [tolerance=±5% resistance=100k power=0.25W package=THT]
  R50 = Resistor [tolerance=±5% resistance=1k package=THT]
  R51 = Resistor [tolerance=±5% resistance=1k package=THT]
  D16 = Zener Diode [part_number=1N5919BG breakdown_voltage=5.1V package="300 mil [THT]"]
  D17 = Schottky Diode [part_number=1N5818 package="300 mil [THT]"]
  R55 = Resistor [tolerance=±5% resistance=100k package=THT]
  R56 = Resistor [tolerance=±5% resistance=100k power=0.25W package=THT]
  R57 = Resistor [tolerance=±5% resistance=1k package=THT]
  R58 = Resistor [tolerance=±5% resistance=1k package=THT]
  LED5 = LED - 3mm [color="Red (633nm)" package="3 mm [THT]"]
  LED6 = LED - 3mm [color="Red (633nm)" package="3 mm [THT]"]
  LED7 = LED - 3mm [color="Red (633nm)" package="3 mm [THT]"]
  LED8 = LED - 3mm [color="Red (633nm)" package="3 mm [THT]"]
  Q5 = Basic FET N-Channel [part_number=STP62NS04Z package="TO220 [THT]"]
  R32 = Resistor [tolerance=±5% resistance=160 power=2W package=THT]
  Q7 = Basic FET N-Channel [part_number=STP62NS04Z package="TO220 [THT]"]
  Q6 = Basic FET N-Channel [part_number=STP62NS04Z package="TO220 [THT]"]
  J4 = shrouded pin header, 40 pins [form="♂ (shrouded male)"]
  Q8 = Basic FET N-Channel [part_number=STP62NS04Z package="TO220 [THT]"]
  C23 = Ceramic Capacitor [capacitance=4.7nF package="200 mil [THT, multilayer]"]
  IC4 = IC, DIP package, 8 pins [chip_label=SP721 part_number=SP721]
  R59 = Resistor [tolerance=±5% resistance=1k package=THT]
  R60 = Resistor [tolerance=±5% resistance=1k package=THT]
  J10 = female pin header, 1 pin [form="♀ (female)"]  # not connected
  J23 = female pin header, 1 pin [form="♀ (female)"]  # not connected
  J35 = female pin header, 1 pin [form="♀ (female)"]
  J45 = female pin header, 1 pin [form="♀ (female)"]  # not connected
  J46 = female pin header, 1 pin [form="♀ (female)"]  # not connected
  J47 = female pin header, 1 pin [form="♀ (female)"]
  J49 = female pin header, 1 pin [form="♀ (female)"]  # not connected
  J50 = female pin header, 1 pin [form="♀ (female)"]
  J57 = female pin header, 1 pin [form="♀ (female)"]
  J58 = female pin header, 1 pin [form="♀ (female)"]
  J60 = female pin header, 1 pin [form="♀ (female)"]
  J61 = female pin header, 1 pin [form="♀ (female)"]
  J62 = female pin header, 1 pin [form="♀ (female)"]
  J63 = female pin header, 1 pin [form="♀ (female)"]  # not connected
  J65 = female pin header, 1 pin [form="♀ (female)"]
  J68 = female pin header, 1 pin [form="♀ (female)"]
  J70 = female pin header, 5 pins [form="♀ (female)"]
  DRV8825 = Pololu A4988 [package=SO16]
  R61 = Resistor [tolerance=±5% resistance=2.49k package=THT]
  C24 = Ceramic Capacitor [capacitance=0.22µF package="200 mil [THT, multilayer]"]
  C25 = Ceramic Capacitor [capacitance=0.01µF package="200 mil [THT, multilayer]"]
  MPX4250AP1 = MPX4250AP pressure sensor [part_number=MPX]
  12v_Jump = ULN2003A [package="DIP16 [THT]"]
  J71 = female pin header, 1 pin [form="♀ (female)"]  # not connected
  J72 = female pin header, 1 pin [form="♀ (female)"]  # not connected
  J73 = female pin header, 1 pin [form="♀ (female)"]  # not connected
  J74 = female pin header, 1 pin [form="♀ (female)"]  # not connected
  J76 = female pin header, 1 pin [form="♀ (female)"]
  J77 = female pin header, 1 pin [form="♀ (female)"]  # not connected
  J78 = female pin header, 1 pin [form="♀ (female)"]  # not connected
  J79 = female pin header, 1 pin [form="♀ (female)"]  # not connected
  J80 = female pin header, 1 pin [form="♀ (female)"]  # not connected
  J81 = female pin header, 1 pin [form="♀ (female)"]  # not connected
  J82 = female pin header, 1 pin [form="♀ (female)"]  # not connected
  J83 = female pin header, 1 pin [form="♀ (female)"]  # not connected
  J84 = female pin header, 1 pin [form="♀ (female)"]  # not connected
  J85 = female pin header, 1 pin [form="♀ (female)"]  # not connected
  J86 = female pin header, 1 pin [form="♀ (female)"]  # not connected
  J87 = female pin header, 1 pin [form="♀ (female)"]  # not connected
  J88 = female pin header, 1 pin [form="♀ (female)"]  # not connected
  J89 = female pin header, 1 pin [form="♀ (female)"]  # not connected
  J90 = female pin header, 1 pin [form="♀ (female)"]  # not connected
  J91 = female pin header, 1 pin [form="♀ (female)"]  # not connected
  J92 = female pin header, 1 pin [form="♀ (female)"]  # not connected
  J93 = female pin header, 1 pin [form="♀ (female)"]  # not connected
  J94 = female pin header, 1 pin [form="♀ (female)"]  # not connected
  J95 = female pin header, 1 pin [form="♀ (female)"]  # not connected
  J96 = female pin header, 1 pin [form="♀ (female)"]  # not connected
  J97 = female pin header, 1 pin [form="♀ (female)"]  # not connected
  J98 = female pin header, 1 pin [form="♀ (female)"]  # not connected
  J99 = female pin header, 1 pin [form="♀ (female)"]  # not connected
  J100 = female pin header, 1 pin [form="♀ (female)"]  # not connected
  J101 = female pin header, 1 pin [form="♀ (female)"]  # not connected
  J103 = female pin header, 1 pin [form="♀ (female)"]
  J109 = female pin header, 3 pins [form="♀ (female)"]
  J111 = female pin header, 1 pin [form="♀ (female)"]  # not connected
  J112 = female pin header, 1 pin [form="♀ (female)"]  # not connected
  J113 = female pin header, 1 pin [form="♀ (female)"]  # not connected
  J114 = female pin header, 1 pin [form="♀ (female)"]
  J115 = female pin header, 1 pin [form="♀ (female)"]  # not connected
  J110 = female pin header, 3 pins [form="♀ (female)"]
  J116 = female pin header, 1 pin [form="♀ (female)"]  # not connected
  J117 = female pin header, 1 pin [form="♀ (female)"]  # not connected
  J118 = female pin header, 1 pin [form="♀ (female)"]  # not connected
  J119 = female pin header, 1 pin [form="♀ (female)"]  # not connected
  J120 = female pin header, 1 pin [form="♀ (female)"]  # not connected
  J121 = female pin header, 1 pin [form="♀ (female)"]  # not connected
  J122 = female pin header, 1 pin [form="♀ (female)"]  # not connected
  J123 = female pin header, 1 pin [form="♀ (female)"]  # not connected
  J124 = female pin header, 1 pin [form="♀ (female)"]  # not connected
  J125 = female pin header, 1 pin [form="♀ (female)"]  # not connected
  J126 = female pin header, 1 pin [form="♀ (female)"]  # not connected
  J127 = female pin header, 1 pin [form="♀ (female)"]  # not connected
  J128 = female pin header, 1 pin [form="♀ (female)"]  # not connected
  J129 = female pin header, 1 pin [form="♀ (female)"]  # not connected
  J130 = female pin header, 1 pin [form="♀ (female)"]  # not connected
  A5_A6_A7 = female pin header, 1 pin [form="♀ (female)"]
  J131 = female pin header, 1 pin [form="♀ (female)"]  # not connected
  J132 = female pin header, 1 pin [form="♀ (female)"]  # not connected
  J133 = female pin header, 1 pin [form="♀ (female)"]  # not connected
  J134 = female pin header, 1 pin [form="♀ (female)"]  # not connected
  J135 = female pin header, 1 pin [form="♀ (female)"]  # not connected
  J136 = female pin header, 1 pin [form="♀ (female)"]  # not connected
  J137 = female pin header, 1 pin [form="♀ (female)"]  # not connected
  J138 = female pin header, 1 pin [form="♀ (female)"]  # not connected
  J139 = female pin header, 1 pin [form="♀ (female)"]  # not connected
  J140 = female pin header, 2 pins [form="♀ (female)"]
  J141 = female pin header, 2 pins [form="♀ (female)"]
  J142 = female pin header, 3 pins [form="♀ (female)"]
  R54 = Resistor [tolerance=±5% resistance=470 package=THT]
  R62 = Resistor [tolerance=±5% resistance=120 package=THT]

nets:
  ADC Clamp1/O2-CPU-A8: Arduino_Mega_2560.A8, R22.Pin_1, C10.1, IC4.pin2
  CPU-A15: Arduino_Mega_2560.A15, J61.pin1
  ADC Clamp6/IAT-CPU-A0: Arduino_Mega_2560.A0, R2.Pin_1, C2.1, IC4.pin7
  ADC Clamp2/CLT-CPU-A1: Arduino_Mega_2560.A1, R4.Pin_1, C4.1, IC4.pin6
  ADC Clamp3/TPS-CPU-A2: Arduino_Mega_2560.A2, R6.Pin_1, C6.1, IC4.pin1
  MAP-CPU-A3: Arduino_Mega_2560.A3, C18.0, R41.Pin_1, J4.pin11
  ADC Clamp4/BRV-CPU-A4: Arduino_Mega_2560.A4, R8.Pin_1, C8.1, IC4.pin5
  N1: Arduino_Mega_2560.A5, A5_A6_A7.pin1
  N2: Arduino_Mega_2560.A6, J35.pin1
  N3: Arduino_Mega_2560.A7, J47.pin1
  SCL-CPU-D21: Arduino_Mega_2560.D21/SCL, Arduino_Mega_2560.SCL, J65.pin1
  ADC Clamp5/TACH1-CPU-D19: Arduino_Mega_2560.D19/RX1, IC3.pin8, JP2.pin1, IC4.pin3, C25.0
  TACH2-CPU-D18: Arduino_Mega_2560.D18/TX1, IC3.pin7, JP3.pin3, C24.0
  STEP-CPU-D17: Arduino_Mega_2560.D17_PWM/RX2, DRV8825.STEP
  STEPDIR-CPU-D16: Arduino_Mega_2560.D16_PWM/TX2, DRV8825.DIR
  SDA-CPU-D20: Arduino_Mega_2560.SDA, J103.pin1
  GND: Arduino_Mega_2560.GND, Q1.source, R11.Pin_1, C7.0, C1.0, C3.0, C5.0, J3.pin1, Q2.source, R17.Pin_1, Q3.source, R14.Pin_1, Q4.source, R20.Pin_1, C2.0, C8.0, R21.Pin_1, C9.0, C6.0, C4.0, C10.0, IC1.pin3, C11.0, IC2.pin3, C12.0, U1.GND, C14.-, C13.0, C15.0, C16.-, U2.P$2, R35.Pin_0, R36.Pin_0, R37.Pin_0, R38.Pin_0, IC3.pin6, C18.1, C19.0, C20.0, R48.Pin_0, R49.Pin_0, D16.anode, R55.Pin_0, R56.Pin_0, LED5.cathode, LED6.cathode, LED7.cathode, LED8.cathode, Q5.source, Q7.source, Q6.source, J4.pin9, J4.pin10, J4.pin12, J4.pin23, Q8.source, C23.0, IC4.pin4, DRV8825.GND, C24.1, C25.1, MPX4250AP1.GND
  INJ4-CPU-D11: Arduino_Mega_2560.D11_PWM, R19.Pin_0, R20.Pin_0
  INJ3-CPU-D10: Arduino_Mega_2560.D10_PWM, R16.Pin_0, R17.Pin_0
  INJ2-CPU-D9: Arduino_Mega_2560.D9_PWM, R13.Pin_0, R14.Pin_0
  INJ1-CPU-D8: Arduino_Mega_2560.D8_PWM, R10.Pin_0, R11.Pin_0
  5V: Arduino_Mega_2560.IOREF, Arduino_Mega_2560.5V, R1.Pin_0, R3.Pin_0, U1.output_voltage, C14.+, C13.1, IC3.pin5, JP1.pin1, R39.Pin_0, R40.Pin_0, C19.1, C20.1, D16.cathode, D17.cathode, J4.pin13, J4.pin28, IC4.pin8, J70.pin1, J70.pin2, J70.pin3, J70.pin4, J70.pin5, DRV8825.RESET, DRV8825.SLEEP, R61.Pin_1, MPX4250AP1.Vs, J109.pin1, J109.pin2, J109.pin3, R54.Pin_1, R62.Pin_1
  RESET: Arduino_Mega_2560.RESET, D17.anode, C23.1, J142.pin2
  N4: Arduino_Mega_2560.D0_RX0, J76.pin1
  N5: Arduino_Mega_2560.D1_TX0, J50.pin1
  CPU-D2: Arduino_Mega_2560.D2_PWM, R61.Pin_0, J114.pin1
  CPU-D4: Arduino_Mega_2560.D4_PWM, R58.Pin_0
  CPU-D5: Arduino_Mega_2560.D5_PWM, R50.Pin_0
  CPU-D6: Arduino_Mega_2560.D6_PWM, R57.Pin_0
  CPU-D7: Arduino_Mega_2560.D7_PWM, R51.Pin_0
  CPU-D24: Arduino_Mega_2560.D24, DRV8825.ENABLE
  IGN2-CPU-D24: Arduino_Mega_2560.D38, R24.Pin_0
  IGN1-CPU-D28: Arduino_Mega_2560.D40, R23.Pin_0
  RST-CPU-D48: Arduino_Mega_2560.D43, J60.pin1, 12v_Jump.In_2
  LC-CPU-D45: Arduino_Mega_2560.D45, J62.pin1, 12v_Jump.In_4
  LC-CPU-D47: Arduino_Mega_2560.D47, J68.pin1, 12v_Jump.In_3
  LC-CPU-D49: Arduino_Mega_2560.D49, J58.pin1, 12v_Jump.In_5
  IGN4-CPU-D36: Arduino_Mega_2560.D50, R30.Pin_0
  LC-CPU-D51: Arduino_Mega_2560.D51, J57.pin1
  IGN3-CPU-D40: Arduino_Mega_2560.D52, R29.Pin_0
  LC-CPU-D53: Arduino_Mega_2560.D53
  IAT Sensor: R1.Pin_1, R2.Pin_0, C1.1, J4.pin20
  CLT Sensor: R3.Pin_1, R4.Pin_0, C3.1, J4.pin19
  TPS Sensor: R6.Pin_0, C5.1, J4.pin22
  12V/12V-raw: R7.Pin_0, J3.pin2, D15.anode, C15.1, C16.+, U2.P$1, JP1.pin3, DRV8825.VMOT
  N6: R7.Pin_1, R8.Pin_0, C7.1, R21.Pin_0
  N7: Q1.gate, R10.Pin_1
  INJ-1-OUT: Q1.drain, J4.pin1, J4.pin40
  N8: Q2.gate, R16.Pin_1
  INJ-3-OUT: Q2.drain, J4.pin3, J4.pin4
  N9: Q3.gate, R13.Pin_1
  INJ-2-OUT: Q3.drain, J4.pin2, J4.pin39
  N10: Q4.gate, R19.Pin_1
  INJ-4-OUT: Q4.drain, J4.pin5, J4.pin6
  O2 Sensor: C9.1, R22.Pin_0, J4.pin21
  N11: IC1.pin2, R23.Pin_1, R37.Pin_1
  N12: IC1.pin4, R24.Pin_1, R35.Pin_1
  N13: IC1.pin5, R25.Pin_0
  JP1-OUT: IC1.pin6, C11.1, IC2.pin6, C12.1, JP1.pin2
  N14: IC1.pin7, R27.Pin_1
  IGN-2-OUT: R25.Pin_1, R26.Pin_1, J4.pin34
  N15: R26.Pin_0, LED6.anode
  IGN-1-OUT: R27.Pin_0, R28.Pin_1, J4.pin7
  N16: R28.Pin_0, LED5.anode
  N17: IC2.pin2, R29.Pin_1, R38.Pin_1
  N18: IC2.pin4, R30.Pin_1, R36.Pin_1
  N19: IC2.pin5, R32.Pin_0
  N20: IC2.pin7, R31.Pin_1
  IGN-3-OUT: R31.Pin_0, R33.Pin_1, J4.pin33
  N21: R33.Pin_0, LED7.anode
  N22: R34.Pin_0, LED8.anode
  IGN-4-OUT: R34.Pin_1, R32.Pin_1, J4.pin8
  N23: U1.input_voltage, D15.cathode, 12v_Jump.COM_-_Common, J140.pin1, J140.pin2
  VR1-: IC3.pin1, J4.pin27
  N24: IC3.pin2, JP2.pin3
  N25: IC3.pin3, JP3.pin1
  VR2-: IC3.pin4, J4.pin26
  N26: JP2.pin2, R59.Pin_1
  N27: JP3.pin2, R60.Pin_1
  N28: R39.Pin_1, JP4.pin1
  VR1+: JP4.pin2, J4.pin25, R59.Pin_0
  N29: R40.Pin_1, JP5.pin2
  VR2+: JP5.pin1, J4.pin24, R60.Pin_0
  N30: R41.Pin_0, MPX4250AP1.V_out
  N31: R48.Pin_1, R50.Pin_1, Q7.gate
  N32: R49.Pin_1, R51.Pin_1, Q8.gate
  N33: R55.Pin_1, R57.Pin_1, Q5.gate
  N34: R56.Pin_1, R58.Pin_1, Q6.gate
  HC-1-OUT: Q5.drain, J4.pin36
  IDLE-OUT: Q7.drain, J4.pin37
  HC-2-OUT: Q6.drain, J4.pin38
  LC-1-OUT: J4.pin14, 12v_Jump.Out_2
  LC-2-OUT: J4.pin15, 12v_Jump.Out_3
  LC-3-OUT: J4.pin16, 12v_Jump.Out_4
  LC-4-OUT: J4.pin17, 12v_Jump.Out_5
  LC-5-OUT: J4.pin18, 12v_Jump.Out_6
  STEP-2B-OUT: J4.pin29, DRV8825.2B
  STEP-2A-OUT: J4.pin30, DRV8825.2A
  STEP-1A-OUT: J4.pin31, DRV8825.1A
  STEP-1B-OUT: J4.pin32, DRV8825.1B
  BOOST-OUT: J4.pin35, Q8.drain
  N35: J110.pin1, J110.pin2, J110.pin3
  N36: J141.pin1, J141.pin2
  N37: J142.pin1, R54.Pin_0
  N38: J142.pin3, R62.Pin_0

notes:
  Inlet Air Temperature sensor
  Coolant Temperature Sensor
  Speeduino v0.4, Throttle Position Sensor
  Battery Reference Voltage
  Injector 1
  Speeduino v0.4, Connector 1
  Injector 3
  Injector 2
  Injector 4
  Speeduino v0.4, O2 Sensor
  Ignitor output 1
  Ignitor output 2
  12v
  5v
  Power supply
  IGN Out
  Crank and Cam sensors
  Speeduino v0.4, MAP sensor input
  DetonationEMS.com
  Generic Outputs - High Current
  inj1
  VR
  Hall
  Reset Protection - Refer AVR040 Application note
  ADC Clamping circuit
  Stepper Driver
  PWM Idle / Boost
  GND
  |12V|
  Gnd
  A15
  51
  49
  45
  47
  43
  21
  20
  5V
  Proto Area
  Flat side down
  ULN2003a
  →
  Eth
  RX
  TX
  |  5v  |
  | GND |
  A5 A6 A7
  |GND|
  Run  Prog
