# Fritzing sketch v1.0.0.0.2 (saved by Fritzing 0.9.4)
circuit board: 10cm x 10cm

parts:
  Arduino_Mega_2560 = Arduino Mega 2560 (Rev3) [part_number="Arduino Mega 2560"]
  Q1 = Basic FET N-Channel [part_number=STP62NS04Z package="TO220 [THT]"]
  Q2 = Basic FET N-Channel [part_number=STP62NS04Z package="TO220 [THT]"]
  Q3 = Basic FET N-Channel [part_number=STP62NS04Z package="TO220 [THT]"]
  Q4 = Basic FET N-Channel [part_number=STP62NS04Z package="TO220 [THT]"]
  U1 = Voltage Regulator - 5V [part_number=LM2940T-5.0 package="TO220 [THT]"]
  D15 = Schottky Diode [part_number=1N5818 package="300 mil [THT]"]
  U2 = V18ZA2P [part_number=ERZV14D220 package=v18za2p]
  IC3 = IC, DIP package, 8 pins [chip_label="Dual VR Conditioner"]
  JP1 = female pin header, 3 pins [form="♀ (female)"]
  JP2 = female pin header, 3 pins [form="♀ (female)"]
  JP3 = female pin header, 3 pins [form="♀ (female)"]
  JP4 = female pin header, 2 pins [form="♀ (female)"]
  JP5 = female pin header, 2 pins [form="♀ (female)"]
  D17 = Schottky Diode [part_number=1N5818 package="300 mil [THT]"]
  Q5 = Basic FET N-Channel [part_number=STP62NS04Z package="TO220 [THT]"]
  Q7 = Basic FET N-Channel [part_number=STP62NS04Z package="TO220 [THT]"]
  Q6 = Basic FET N-Channel [part_number=STP62NS04Z package="TO220 [THT]"]
  J4 = shrouded pin header, 40 pins [form="♂ (shrouded male)"]
  Q8 = Basic FET N-Channel [part_number=STP62NS04Z package="TO220 [THT]"]
  J45 = female pin header, 1 pin [form="♀ (female)"]  # not connected
  J46 = female pin header, 1 pin [form="♀ (female)"]  # not connected
  J49 = female pin header, 1 pin [form="♀ (female)"]  # not connected
  J50 = female pin header, 1 pin [form="♀ (female)"]
  J57 = female pin header, 1 pin [form="♀ (female)"]
  J58 = female pin header, 1 pin [form="♀ (female)"]
  J60 = female pin header, 1 pin [form="♀ (female)"]
  J62 = female pin header, 1 pin [form="♀ (female)"]
  J63 = female pin header, 1 pin [form="♀ (female)"]  # not connected
  J68 = female pin header, 1 pin [form="♀ (female)"]
  DRV8825 = Pololu A4988 [package=SO16]
  J71 = female pin header, 1 pin [form="♀ (female)"]  # not connected
  J72 = female pin header, 1 pin [form="♀ (female)"]  # not connected
  J73 = female pin header, 1 pin [form="♀ (female)"]  # not connected
  J74 = female pin header, 1 pin [form="♀ (female)"]  # not connected
  J76 = female pin header, 1 pin [form="♀ (female)"]
  J77 = female pin header, 1 pin [form="♀ (female)"]  # not connected
  J78 = female pin header, 1 pin [form="♀ (female)"]  # not connected
  J79 = female pin header, 1 pin [form="♀ (female)"]  # not connected
  J80 = female pin header, 1 pin [form="♀ (female)"]  # not connected
  J81 = female pin header, 1 pin [form="♀ (female)"]  # not connected
  J82 = female pin header, 1 pin [form="♀ (female)"]  # not connected
  J83 = female pin header, 1 pin [form="♀ (female)"]  # not connected
  J84 = female pin header, 1 pin [form="♀ (female)"]  # not connected
  J85 = female pin header, 1 pin [form="♀ (female)"]  # not connected
  J86 = female pin header, 1 pin [form="♀ (female)"]  # not connected
  J87 = female pin header, 1 pin [form="♀ (female)"]  # not connected
  J90 = female pin header, 1 pin [form="♀ (female)"]  # not connected
  J92 = female pin header, 1 pin [form="♀ (female)"]  # not connected
  J93 = female pin header, 1 pin [form="♀ (female)"]  # not connected
  J94 = female pin header, 1 pin [form="♀ (female)"]  # not connected
  J95 = female pin header, 1 pin [form="♀ (female)"]  # not connected
  J96 = female pin header, 1 pin [form="♀ (female)"]  # not connected
  J111 = female pin header, 1 pin [form="♀ (female)"]  # not connected
  J112 = female pin header, 1 pin [form="♀ (female)"]
  J113 = female pin header, 1 pin [form="♀ (female)"]  # not connected
  J114 = female pin header, 1 pin [form="♀ (female)"]
  J119 = female pin header, 1 pin [form="♀ (female)"]  # not connected
  J123 = female pin header, 1 pin [form="♀ (female)"]  # not connected
  J124 = female pin header, 1 pin [form="♀ (female)"]  # not connected
  J125 = female pin header, 1 pin [form="♀ (female)"]
  J142 = female pin header, 3 pins [form="♀ (female)"]
  J143 = female pin header, 1 pin [form="♀ (female)"]  # not connected
  J144 = female pin header, 1 pin [form="♀ (female)"]  # not connected
  J145 = female pin header, 1 pin [form="♀ (female)"]
  J109 = female pin header, 4 pins [form="♀ (female)"]
  J110 = female pin header, 4 pins [form="♀ (female)"]  # not connected
  J3 = screw terminal, 2 pins
  MPX4250AP1 = MPX4250AP pressure sensor [part_number=MPX]
  C5 = Ceramic Capacitor [capacitance=0.1µF package="0805 [SMD, multilayer]"]
  C20 = Ceramic Capacitor [capacitance=1µF package="0805 [SMD, multilayer]"]
  LED3 = smd LED [color="Red (633nm)" package="0805 [SMD]"]
  LED4 = smd LED [color="Red (633nm)" package="0805 [SMD]"]
  C12 = Ceramic Capacitor [capacitance=1µF package="0805 [SMD, multilayer]"]
  C4 = Ceramic Capacitor [capacitance=0.22µF package="0805 [SMD, multilayer]"]
  R62 = Resistor [tolerance=±5% resistance=120 package="0805 [SMD]"]
  C2 = Ceramic Capacitor [capacitance=0.22µF package="0805 [SMD, multilayer]"]
  C1 = Ceramic Capacitor [capacitance=0.1µF package="0805 [SMD, multilayer]"]
  C23 = Ceramic Capacitor [capacitance=4.7nF package="0603 [SMD, multilayer]"]
  R7 = Resistor [tolerance=±0.1% resistance=3.9k package="0805 [SMD]"]
  R1 = Resistor [tolerance=±0.1% resistance=2.49k package="0805 [SMD]"]
  C8 = Ceramic Capacitor [capacitance=0.22µF package="0805 [SMD, multilayer]"]
  C7 = Ceramic Capacitor [capacitance=0.1µF package="0805 [SMD, multilayer]"]
  R59 = Resistor [tolerance=±5% resistance=1k package="0805 [SMD]"]
  R40 = Resistor [tolerance=±5% resistance=1k package="0805 [SMD]"]
  R39 = Resistor [tolerance=±5% resistance=1k package="0805 [SMD]"]
  R60 = Resistor [tolerance=±5% resistance=1k package="0805 [SMD]"]
  C24 = Ceramic Capacitor [capacitance=0.22µF package="0805 [SMD, multilayer]"]
  R3 = Resistor [tolerance=±0.1% resistance=2.49k package="0805 [SMD]"]
  C10 = Ceramic Capacitor [capacitance=0.22µF package="0805 [SMD, multilayer]"]
  C9 = Ceramic Capacitor [capacitance=0.1µF package="0805 [SMD, multilayer]"]
  C25 = Ceramic Capacitor [capacitance=0.01µF package="0805 [SMD, multilayer]"]
  C3 = Ceramic Capacitor [capacitance=0.1µF package="0805 [SMD, multilayer]"]
  R2 = Resistor [tolerance=±5% resistance=470 package="0805 [SMD]"]
  R4 = Resistor [tolerance=±5% resistance=470 package="0805 [SMD]"]
  R54 = Resistor [tolerance=±5% resistance=470 package="0805 [SMD]"]
  R22 = Resistor [tolerance=±5% resistance=470 package="0805 [SMD]"]
  R6 = Resistor [tolerance=±5% resistance=470 package="0805 [SMD]"]
  C6 = Ceramic Capacitor [capacitance=0.22µF package="0805 [SMD, multilayer]"]
  R33 = Resistor [tolerance=±5% resistance=2.4k power=0.25W package="0805 [SMD]"]
  R31 = Resistor [tolerance=±5% resistance=10 power=1 package="0805 [SMD]"]
  R34 = Resistor [tolerance=±5% resistance=2.4k package="0805 [SMD]"]
  R32 = Resistor [tolerance=±5% resistance=10 power=2W package="0805 [SMD]"]
  R8 = Resistor [tolerance=±5% resistance=470 package="0805 [SMD]"]
  R21 = Resistor [tolerance=±5% resistance=1k package="0805 [SMD]"]
  IC4 = SSOP16 [chip_label=SP720 package=SSOP]
  R49 = Resistor [tolerance=±5% resistance=100k power=0.25W package="0805 [SMD]"]
  R55 = Resistor [tolerance=±5% resistance=100k package="0805 [SMD]"]
  R48 = Resistor [tolerance=±5% resistance=100k package="0805 [SMD]"]
  R56 = Resistor [tolerance=±5% resistance=100k power=0.25W package="0805 [SMD]"]
  R51 = Resistor [tolerance=±5% resistance=1k package="0805 [SMD]"]
  R57 = Resistor [tolerance=±5% resistance=1k package="0805 [SMD]"]
  R50 = Resistor [tolerance=±5% resistance=1k package="0805 [SMD]"]
  R58 = Resistor [tolerance=±5% resistance=1k package="0805 [SMD]"]
  LED2 = smd LED [color="Red (633nm)" package="0805 [SMD]"]
  R28 = Resistor [tolerance=±5% resistance=2.4k package="0805 [SMD]"]
  R26 = Resistor [tolerance=±5% resistance=2.4k package="0805 [SMD]"]
  R27 = Resistor [tolerance=±5% resistance=160 power=2W package="0805 [SMD]"]
  R25 = Resistor [tolerance=±5% resistance=10 power=2W package="0805 [SMD]"]
  R35 = Resistor [tolerance=±5% resistance=100k package="0805 [SMD]"]
  R37 = Resistor [tolerance=±5% resistance=100k package="0805 [SMD]"]
  R23 = Resistor [tolerance=±5% resistance=1k package="0805 [SMD]"]
  R24 = Resistor [tolerance=±5% resistance=1k package="0805 [SMD]"]
  C11 = Ceramic Capacitor [capacitance=1µF package="0805 [SMD, multilayer]"]
  R38 = Resistor [tolerance=±5% resistance=100k package="0805 [SMD]"]
  R29 = Resistor [tolerance=±5% resistance=1k package="0805 [SMD]"]
  R30 = Resistor [tolerance=±5% resistance=1k package="0805 [SMD]"]
  R36 = Resistor [tolerance=±5% resistance=100k package="0805 [SMD]"]
  R9 = Resistor [tolerance=±5% resistance=100k package="0805 [SMD]"]
  R12 = Resistor [tolerance=±5% resistance=1k power=0.25W package="0805 [SMD]"]
  R10 = Resistor [tolerance=±5% resistance=100k power=0.25W package="0805 [SMD]"]
  R11 = Resistor [tolerance=±5% resistance=1k package="0805 [SMD]"]
  R13 = Resistor [tolerance=±5% resistance=100k package="0805 [SMD]"]
  R15 = Resistor [tolerance=±5% resistance=1k package="0805 [SMD]"]
  R14 = Resistor [tolerance=±5% resistance=100k package="0805 [SMD]"]
  R16 = Resistor [tolerance=±5% resistance=1k package="0805 [SMD]"]
  R41 = Resistor [tolerance=±5% resistance=470 package="0805 [SMD]"]
  C19 = Ceramic Capacitor [capacitance=0.01µF package="0805 [SMD, multilayer]"]
  12v_Jump = ULN2003A [package="SO16 [SMD]"]
  JP6 = female pin header, 4 pins [form="♀ (female)"]
  R61 = Resistor [tolerance=±5% resistance=2.49k package="0805 [SMD]"]
  C15 = Ceramic Capacitor [capacitance=0.1µF voltage=50V package="0805 [SMD, multilayer]"]
  C13 = Ceramic Capacitor [capacitance=0.1µF voltage=50V package="0805 [SMD, multilayer]"]
  J169 = female pin header, 1 pin [form="♀ (female)"]  # not connected
  J170 = female pin header, 1 pin [form="♀ (female)"]  # not connected
  J171 = female pin header, 1 pin [form="♀ (female)"]  # not connected
  J172 = female pin header, 1 pin [form="♀ (female)"]  # not connected
  J173 = female pin header, 1 pin [form="♀ (female)"]  # not connected
  J174 = female pin header, 1 pin [form="♀ (female)"]  # not connected
  J175 = female pin header, 1 pin [form="♀ (female)"]  # not connected
  J176 = female pin header, 1 pin [form="♀ (female)"]  # not connected
  J177 = female pin header, 1 pin [form="♀ (female)"]  # not connected
  J178 = female pin header, 1 pin [form="♀ (female)"]  # not connected
  J179 = female pin header, 1 pin [form="♀ (female)"]  # not connected
  J180 = female pin header, 1 pin [form="♀ (female)"]  # not connected
  J181 = female pin header, 1 pin [form="♀ (female)"]  # not connected
  J182 = female pin header, 1 pin [form="♀ (female)"]  # not connected
  J183 = female pin header, 1 pin [form="♀ (female)"]  # not connected
  J184 = female pin header, 1 pin [form="♀ (female)"]  # not connected
  J185 = female pin header, 1 pin [form="♀ (female)"]  # not connected
  J186 = female pin header, 1 pin [form="♀ (female)"]  # not connected
  J187 = female pin header, 1 pin [form="♀ (female)"]  # not connected
  J188 = female pin header, 1 pin [form="♀ (female)"]  # not connected
  J189 = female pin header, 1 pin [form="♀ (female)"]  # not connected
  J190 = female pin header, 1 pin [form="♀ (female)"]  # not connected
  J191 = female pin header, 1 pin [form="♀ (female)"]  # not connected
  J192 = female pin header, 1 pin [form="♀ (female)"]  # not connected
  J193 = female pin header, 1 pin [form="♀ (female)"]  # not connected
  J194 = female pin header, 1 pin [form="♀ (female)"]  # not connected
  J195 = female pin header, 1 pin [form="♀ (female)"]  # not connected
  J196 = female pin header, 1 pin [form="♀ (female)"]  # not connected
  J197 = female pin header, 1 pin [form="♀ (female)"]  # not connected
  J198 = female pin header, 1 pin [form="♀ (female)"]  # not connected
  J199 = female pin header, 1 pin [form="♀ (female)"]  # not connected
  J200 = female pin header, 1 pin [form="♀ (female)"]  # not connected
  R63 = Resistor [tolerance=±5% resistance=10k package=THT]
  IC2 = IC, DIP package, 8 pins [chip_label=IC]
  IC1 = IC, DIP package, 8 pins [chip_label=IC]
  LED1 = smd LED [color="Red (633nm)" package="0805 [SMD]"]
  C18 = Ceramic Capacitor [capacitance=10pF package="200 mil [THT, multilayer]"]
  C14 = Tantalum Capacitor [capacitance=47µF voltage=10V package="C 6032 [SMD, tantalum]"]
  C16 = Tantalum Capacitor [capacitance=10µF voltage=35V package="200 mil [THT, tantalum]"]
  D16 = Schottky Diode [part_number=1N5818 package="300 mil [THT]"]

nets (from the pcb view):
  N1: Arduino_Mega_2560.A8, C10.1, R22.Pin_1, IC4.9
  N2: Arduino_Mega_2560.A9, JP6.pin4
  N3: Arduino_Mega_2560.A10, JP6.pin3
  N4: Arduino_Mega_2560.A11, JP6.pin2
  N5: Arduino_Mega_2560.A12, JP6.pin1
  N6: Arduino_Mega_2560.A0, C2.1, R2.Pin_1, IC4.1
  N7: Arduino_Mega_2560.A1, C4.1, R4.Pin_1, IC4.2
  N8: Arduino_Mega_2560.A2, R6.Pin_1, C6.1, IC4.3
  N9: Arduino_Mega_2560.A3, J4.pin11, R41.Pin_1, C18.0
  N10: Arduino_Mega_2560.A4, C8.0, R8.Pin_1, IC4.4
  N11: Arduino_Mega_2560.D21/SCL, Arduino_Mega_2560.SCL, J112.pin1
  N12: Arduino_Mega_2560.D19/RX1, IC3.pin8, JP2.pin1, C25.0, IC4.5
  N13: Arduino_Mega_2560.D18/TX1, IC3.pin7, JP3.pin3, C24.0, IC4.10
  N14: Arduino_Mega_2560.D17_PWM/RX2, DRV8825.STEP
  N15: Arduino_Mega_2560.D16_PWM/TX2, DRV8825.DIR
  N16: Arduino_Mega_2560.SDA, J125.pin1
  N17: Arduino_Mega_2560.D11_PWM, R14.Pin_0, R16.Pin_0
  N18: Arduino_Mega_2560.D10_PWM, R13.Pin_0, R15.Pin_0
  N19: Arduino_Mega_2560.D9_PWM, R12.Pin_0, R10.Pin_0
  N20: Arduino_Mega_2560.D8_PWM, R9.Pin_0, R11.Pin_0
  N21: Arduino_Mega_2560.RESET, D17.anode, J142.pin2, C23.1
  N22: Arduino_Mega_2560.5V, U1.output_voltage, IC3.pin5, JP1.pin1, D17.cathode, J4.pin13, J4.pin28, DRV8825.RESET, DRV8825.SLEEP, J109.pin1, J109.pin2, J109.pin3, J109.pin4, MPX4250AP1.Vs, C20.1, R62.Pin_1, R1.Pin_0, R40.Pin_0, R39.Pin_0, R3.Pin_0, R54.Pin_1, IC4.16, C19.1, R61.Pin_1, C13.1, C14.+, D16.anode
  N23: Arduino_Mega_2560.D0_RX0, J76.pin1
  N24: Arduino_Mega_2560.D1_TX0, J50.pin1
  N25: Arduino_Mega_2560.D2_PWM, J114.pin1, R61.Pin_0
  N26: Arduino_Mega_2560.D3_PWM, J145.pin1
  N27: Arduino_Mega_2560.D4_PWM, R58.Pin_0
  N28: Arduino_Mega_2560.D5_PWM, R50.Pin_0
  N29: Arduino_Mega_2560.D6_PWM, R57.Pin_0
  N30: Arduino_Mega_2560.D7_PWM, R51.Pin_0
  N31: Arduino_Mega_2560.D24, DRV8825.ENABLE
  N32: Arduino_Mega_2560.D38, R24.Pin_0
  N33: Arduino_Mega_2560.D40, R23.Pin_0
  N34: Arduino_Mega_2560.D43, J60.pin1, 12v_Jump.In_2
  N35: Arduino_Mega_2560.D45, J62.pin1, 12v_Jump.In_4
  N36: Arduino_Mega_2560.D47, J68.pin1, 12v_Jump.In_3
  N37: Arduino_Mega_2560.D49, J58.pin1, 12v_Jump.In_5
  N38: Arduino_Mega_2560.D50, R30.Pin_0
  N39: Arduino_Mega_2560.D51, J4.pin18, J57.pin1
  N40: Arduino_Mega_2560.D52, R29.Pin_0
  N41: Q1.gate, R11.Pin_1
  N42: Q1.drain, J4.pin1, J4.pin40
  N43: Q2.gate, R15.Pin_1
  N44: Q2.drain, J4.pin3, J4.pin4
  N45: Q3.gate, R12.Pin_1
  N46: Q3.drain, J4.pin2, J4.pin39
  N47: Q4.gate, R16.Pin_1
  N48: Q4.drain, J4.pin5, J4.pin6
  N49: U1.input_voltage, D15.cathode
  N50: D15.anode, U2.P$1, JP1.pin3, DRV8825.VMOT, J3.pin2, R7.Pin_0, 12v_Jump.COM_-_Common, C15.1, R63.Pin_1, C16.+
  N51: IC3.pin1, J4.pin27
  N52: IC3.pin2, JP2.pin3
  N53: IC3.pin3, JP3.pin1
  N54: IC3.pin4, J4.pin26
  N55: JP1.pin2, C12.1, C11.1, IC2.pin6, IC1.pin6
  N56: JP2.pin2, R59.Pin_1
  N57: JP3.pin2, R60.Pin_1
  N58: JP4.pin1, R39.Pin_1
  N59: JP4.pin2, J4.pin25, R59.Pin_0
  N60: JP5.pin1, J4.pin24, R60.Pin_0
  N61: JP5.pin2, R40.Pin_1
  N62: Q5.gate, R55.Pin_1, R57.Pin_1
  N63: Q5.drain, J4.pin36
  N64: Q7.gate, R48.Pin_1, R50.Pin_1
  N65: Q7.drain, J4.pin37
  N66: Q6.gate, R56.Pin_1, R58.Pin_1
  N67: Q6.drain, J4.pin38
  N68: J4.pin7, R28.Pin_1, R27.Pin_0
  N69: J4.pin8, R34.Pin_1, R32.Pin_1
  N70: J4.pin14, 12v_Jump.Out_2
  N71: J4.pin15, 12v_Jump.Out_3
  N72: J4.pin16, 12v_Jump.Out_4
  N73: J4.pin17, 12v_Jump.Out_5, R63.Pin_0
  N74: J4.pin19, R3.Pin_1, C3.1, R4.Pin_0
  N75: J4.pin20, C1.1, R1.Pin_1, R2.Pin_0
  N76: J4.pin21, C9.1, R22.Pin_0
  N77: J4.pin22, C5.1, R6.Pin_0
  N78: J4.pin29, DRV8825.2B
  N79: J4.pin30, DRV8825.2A
  N80: J4.pin31, DRV8825.1A
  N81: J4.pin32, DRV8825.1B
  N82: J4.pin33, R33.Pin_1, R31.Pin_0
  N83: J4.pin34, R26.Pin_1, R25.Pin_1
  N84: J4.pin35, Q8.drain
  N85: Q8.gate, R49.Pin_1, R51.Pin_1
  N86: J142.pin1, R54.Pin_0
  N87: J142.pin3, R62.Pin_0
  N88: MPX4250AP1.V_out, R41.Pin_0
  N89: LED3.anode, R34.Pin_0
  N90: LED4.anode, R33.Pin_0
  N91: R7.Pin_1, C7.1, R8.Pin_0, R21.Pin_0
  N92: R31.Pin_1, IC2.pin7
  N93: R32.Pin_0, IC2.pin5
  N94: LED2.anode, R28.Pin_0
  N95: R26.Pin_0, LED1.anode
  N96: R27.Pin_1, IC1.pin7
  N97: R25.Pin_0, IC1.pin5
  N98: R35.Pin_1, R24.Pin_1, IC1.pin4
  N99: R37.Pin_1, R23.Pin_1, IC1.pin2
  N100: R38.Pin_1, R29.Pin_1, IC2.pin2
  N101: R30.Pin_1, R36.Pin_1, IC2.pin4

notes:
  Inlet Air Temperature sensor
  Coolant Temperature Sensor
  Speeduino v0.4, Throttle Position Sensor
  Battery Reference Voltage
  Injector 1
  Speeduino v0.4, Connector 1
  Injector 3
  Injector 2
  Injector 4
  Speeduino v0.4, O2 Sensor
  Ignitor output 1
  12v
  5v
  Power supply
  IGN Out
  Crank and Cam sensors
  Speeduino v0.4, MAP sensor input
  DetonationEMS.com
  Generic Outputs - High Current
  inj1
  VR
  Hall
  Reset Protection - Refer AVR040 Application note
  Stepper Driver
  PWM Idle / Boost
  GND
  51
  49
  45
  47
  43
  Proto Area
  Flat side down
  ULN2003a
  →
  Eth
  RX
  TX
  5v   |
  |   GND  |
  Run  Prog
  D12 D13
  D3
  v1.1b
  Aaron S. 2020
  SCL SDA
