# Fritzing sketch v1.0.6.6 (saved by Fritzing 0.9.4)
circuit board: 10cm x 10cm
breadboards: 1

parts:
  Arduino_Mega_2560 = Arduino Mega 2560 (Rev3) [part_number="Arduino Mega 2560"]
  R1 = Resistor [tolerance=±0.1% resistance=2.49k part_number=RC55Y-2K49BI package=THT]
  R2 = Resistor [tolerance=±5% resistance=470 package=THT]
  R3 = Resistor [tolerance=±0.1% resistance=2.49k part_number=RC55Y-2K49BI package=THT]
  R4 = Resistor [tolerance=±5% resistance=470 package=THT]
  R6 = Resistor [tolerance=±5% resistance=470 package=THT]
  R7 = Resistor [tolerance=±0.1% resistance=3.9k package=THT]
  R8 = Resistor [tolerance=±5% resistance=470 package=THT]
  Q1 = Basic FET N-Channel [part_number=STP62NS04Z package="TO220 [THT]"]
  R11 = Resistor [tolerance=±5% resistance=1k package=THT]
  R9 = Resistor [tolerance=±5% resistance=100k package=THT]
  C7 = Ceramic Capacitor [capacitance=0.1µF package="200 mil [THT, multilayer]"]
  C1 = Ceramic Capacitor [capacitance=0.1µF package="200 mil [THT, multilayer]"]
  C3 = Ceramic Capacitor [capacitance=0.1µF package="200 mil [THT, multilayer]"]
  C5 = Ceramic Capacitor [capacitance=0.1µF package="200 mil [THT, multilayer]"]
  Q2 = Basic FET N-Channel [part_number=STP62NS04Z package="TO220 [THT]"]
  R15 = Resistor [tolerance=±5% resistance=1k package=THT]
  R13 = Resistor [tolerance=±5% resistance=100k package=THT]
  Q3 = Basic FET N-Channel [part_number=STP62NS04Z package="TO220 [THT]"]
  R12 = Resistor [tolerance=±5% resistance=1k power=0.25W package=THT]
  R10 = Resistor [tolerance=±5% resistance=100k power=0.25W package=THT]
  Q4 = Basic FET N-Channel [part_number=STP62NS04Z package="TO220 [THT]"]
  R16 = Resistor [tolerance=±5% resistance=1k package=THT]
  R14 = Resistor [tolerance=±5% resistance=100k package=THT]
  C2 = Ceramic Capacitor [capacitance=0.22µF package="200 mil [THT, multilayer]"]
  C8 = Ceramic Capacitor [capacitance=0.22µF package="200 mil [THT, multilayer]"]
  R21 = Resistor [tolerance=±5% resistance=1k package=THT]
  C9 = Ceramic Capacitor [capacitance=0.1µF package="200 mil [THT, multilayer]"]
  R22 = Resistor [tolerance=±5% resistance=470 package=THT]
  C6 = Ceramic Capacitor [capacitance=0.22µF package="200 mil [THT, multilayer]"]
  C4 = Ceramic Capacitor [capacitance=0.22µF package="200 mil [THT, multilayer]"]
  C10 = Ceramic Capacitor [capacitance=0.22µF package="200 mil [THT, multilayer]"]
  IC1 = IC, DIP package, 8 pins [chip_label=IC part_number=TC4424EPA]
  R23 = Resistor [tolerance=±5% resistance=1k package=THT]
  R24 = Resistor [tolerance=±5% resistance=1k package=THT]
  C11 = Ceramic Capacitor [capacitance=1µF package="200 mil [THT, multilayer]"]
  R25 = Resistor [tolerance=±5% resistance=10 power=2W package=THT]
  R26 = Resistor [tolerance=±5% resistance=2.4k package=THT]
  R27 = Resistor [tolerance=±5% resistance=160 power=2W package=THT]
  R28 = Resistor [tolerance=±5% resistance=2.4k package=THT]
  IC2 = IC, DIP package, 8 pins [chip_label=IC part_number=TC4424EPA]
  R29 = Resistor [tolerance=±5% resistance=1k package=THT]
  R30 = Resistor [tolerance=±5% resistance=1k package=THT]
  C12 = Ceramic Capacitor [capacitance=1µF package="200 mil [THT, multilayer]"]
  R33 = Resistor [tolerance=±5% resistance=2.4k power=0.25W package=THT]
  R34 = Resistor [tolerance=±5% resistance=2.4k package=THT]
  U1 = Voltage Regulator - 5V [part_number=LM2940T-5.0 package="TO220 [THT]"]
  D15 = Schottky Diode [part_number=1N5818 package="300 mil [THT]"]
  C14 = Tantalum Capacitor [capacitance=47µF voltage=10V package="200 mil [THT, tantalum]"]
  C13 = Ceramic Capacitor [capacitance=0.1µF voltage=50V package="200 mil [THT, multilayer]"]
  C15 = Ceramic Capacitor [capacitance=0.1µF voltage=50V package="200 mil [THT, multilayer]"]
  C16 = Tantalum Capacitor [capacitance=10µF voltage=35V package="200 mil [THT, tantalum]"]
  U2 = V18ZA2P [part_number=ERZV14D220 package=v18za2p]
  R35 = Resistor [tolerance=±5% resistance=100k package=THT]
  R36 = Resistor [tolerance=±5% resistance=100k package=THT]
  R37 = Resistor [tolerance=±5% resistance=100k package=THT]
  R38 = Resistor [tolerance=±5% resistance=100k package=THT]
  IC3 = IC, DIP package, 8 pins [chip_label="Dual VR Conditioner"]
  JP1 = female pin header, 3 pins [form="♀ (female)"]
  JP2 = female pin header, 3 pins [form="♀ (female)"]
  JP3 = female pin header, 3 pins [form="♀ (female)"]
  R39 = Resistor [tolerance=±5% resistance=1k package=THT]
  JP4 = female pin header, 2 pins [form="♀ (female)"]
  R40 = Resistor [tolerance=±5% resistance=1k package=THT]
  JP5 = female pin header, 2 pins [form="♀ (female)"]
  C18 = Ceramic Capacitor [capacitance=0.3µF package="200 mil [THT, multilayer]"]
  R41 = Resistor [tolerance=±5% resistance=470 package=THT]
  C19 = Ceramic Capacitor [capacitance=0.01µF package="200 mil [THT, multilayer]"]
  C20 = Ceramic Capacitor [capacitance=1µF package="200 mil [THT, multilayer]"]
  R48 = Resistor [tolerance=±5% resistance=100k package=THT]
  R49 = Resistor [tolerance=±5% resistance=100k power=0.25W package=THT]
  R50 = Resistor [tolerance=±5% resistance=1k package=THT]
  R51 = Resistor [tolerance=±5% resistance=1k package=THT]
  D16 = Zener Diode [part_number=1N5919BG breakdown_voltage=5.1V package="300 mil [THT]"]
  D17 = Schottky Diode [part_number=1N5818 package="300 mil [THT]"]
  R55 = Resistor [tolerance=±5% resistance=100k package=THT]
  R56 = Resistor [tolerance=±5% resistance=100k power=0.25W package=THT]
  R57 = Resistor [tolerance=±5% resistance=1k package=THT]
  R58 = Resistor [tolerance=±5% resistance=1k package=THT]
  LED1 = LED - 3mm [color="Red (633nm)" package="3 mm [THT]"]
  LED2 = LED - 3mm [color="Red (633nm)" package="3 mm [THT]"]
  LED3 = LED - 3mm [color="Red (633nm)" package="3 mm [THT]"]
  LED4 = LED - 3mm [color="Red (633nm)" package="3 mm [THT]"]
  Q5 = Basic FET N-Channel [part_number=STP62NS04Z package="TO220 [THT]"]
  R32 = Resistor [tolerance=±5% resistance=10 power=2W package=THT]
  Q7 = Basic FET N-Channel [part_number=STP62NS04Z package="TO220 [THT]"]
  Q6 = Basic FET N-Channel [part_number=STP62NS04Z package="TO220 [THT]"]
  J4 = shrouded pin header, 40 pins [form="♂ (shrouded male)"]
  Q8 = Basic FET N-Channel [part_number=STP62NS04Z package="TO220 [THT]"]
  C23 = Ceramic Capacitor [capacitance=4.7nF package="200 mil [THT, multilayer]"]
  R59 = Resistor [tolerance=±5% resistance=220 package=THT]
  J10 = female pin header, 1 pin [form="♀ (female)"]  # not connected
  J23 = female pin header, 1 pin [form="♀ (female)"]  # not connected
  J45 = female pin header, 1 pin [form="♀ (female)"]  # not connected
  J46 = female pin header, 1 pin [form="♀ (female)"]  # not connected
  J49 = female pin header, 1 pin [form="♀ (female)"]  # not connected
  J50 = female pin header, 1 pin [form="♀ (female)"]
  J57 = female pin header, 1 pin [form="♀ (female)"]
  J58 = female pin header, 1 pin [form="♀ (female)"]
  J60 = female pin header, 1 pin [form="♀ (female)"]
  J62 = female pin header, 1 pin [form="♀ (female)"]
  J63 = female pin header, 1 pin [form="♀ (female)"]  # not connected
  J68 = female pin header, 1 pin [form="♀ (female)"]
  DRV8825 = Pololu A4988 [package=SO16]
  R61 = Resistor [tolerance=±5% resistance=2.49k package=THT]
  C24 = Ceramic Capacitor [capacitance=0.1µF package="200 mil [THT, multilayer]"]
  C25 = Ceramic Capacitor [capacitance=0.01µF package="200 mil [THT, multilayer]"]
  MPX4250AP1 = MPX4250AP pressure sensor [part_number=MPX]
  12v_Jump = ULN2003A [package="DIP16 [THT]"]
  J71 = female pin header, 1 pin [form="♀ (female)"]  # not connected
  J72 = female pin header, 1 pin [form="♀ (female)"]  # not connected
  J73 = female pin header, 1 pin [form="♀ (female)"]  # not connected
  J74 = female pin header, 1 pin [form="♀ (female)"]  # not connected
  J76 = female pin header, 1 pin [form="♀ (female)"]
  J77 = female pin header, 1 pin [form="♀ (female)"]  # not connected
  J78 = female pin header, 1 pin [form="♀ (female)"]  # not connected
  J79 = female pin header, 1 pin [form="♀ (female)"]  # not connected
  J80 = female pin header, 1 pin [form="♀ (female)"]  # not connected
  J81 = female pin header, 1 pin [form="♀ (female)"]  # not connected
  J82 = female pin header, 1 pin [form="♀ (female)"]  # not connected
  J83 = female pin header, 1 pin [form="♀ (female)"]  # not connected
  J84 = female pin header, 1 pin [form="♀ (female)"]  # not connected
  J85 = female pin header, 1 pin [form="♀ (female)"]  # not connected
  J86 = female pin header, 1 pin [form="♀ (female)"]  # not connected
  J87 = female pin header, 1 pin [form="♀ (female)"]  # not connected
  J89 = female pin header, 1 pin [form="♀ (female)"]  # not connected
  J90 = female pin header, 1 pin [form="♀ (female)"]  # not connected
  J92 = female pin header, 1 pin [form="♀ (female)"]  # not connected
  J93 = female pin header, 1 pin [form="♀ (female)"]  # not connected
  J94 = female pin header, 1 pin [form="♀ (female)"]  # not connected
  J95 = female pin header, 1 pin [form="♀ (female)"]  # not connected
  J96 = female pin header, 1 pin [form="♀ (female)"]  # not connected
  J111 = female pin header, 1 pin [form="♀ (female)"]  # not connected
  J112 = female pin header, 1 pin [form="♀ (female)"]  # not connected
  J113 = female pin header, 1 pin [form="♀ (female)"]  # not connected
  J114 = female pin header, 1 pin [form="♀ (female)"]
  J119 = female pin header, 1 pin [form="♀ (female)"]  # not connected
  J123 = female pin header, 1 pin [form="♀ (female)"]  # not connected
  J124 = female pin header, 1 pin [form="♀ (female)"]  # not connected
  J125 = female pin header, 1 pin [form="♀ (female)"]  # not connected
  J128 = female pin header, 1 pin [form="♀ (female)"]
  J129 = female pin header, 1 pin [form="♀ (female)"]
  J131 = female pin header, 1 pin [form="♀ (female)"]  # not connected
  J132 = female pin header, 1 pin [form="♀ (female)"]  # not connected
  J133 = female pin header, 1 pin [form="♀ (female)"]  # not connected
  J134 = female pin header, 1 pin [form="♀ (female)"]  # not connected
  J135 = female pin header, 1 pin [form="♀ (female)"]  # not connected
  J136 = female pin header, 1 pin [form="♀ (female)"]  # not connected
  J137 = female pin header, 1 pin [form="♀ (female)"]  # not connected
  J138 = female pin header, 1 pin [form="♀ (female)"]  # not connected
  J139 = female pin header, 1 pin [form="♀ (female)"]  # not connected
  J142 = female pin header, 3 pins [form="♀ (female)"]
  R54 = Resistor [tolerance=±5% resistance=470 package=THT]
  R62 = Resistor [tolerance=±5% resistance=120 package=THT]
  J143 = female pin header, 1 pin [form="♀ (female)"]
  J144 = female pin header, 1 pin [form="♀ (female)"]
  J145 = female pin header, 1 pin [form="♀ (female)"]
  R63 = Resistor [tolerance=±5% resistance=10k package=THT]
  R31 = Resistor [tolerance=±5% resistance=10 power=1 package=THT]
  J140 = female pin header, 2 pins [form="♀ (female)"]
  J109 = female pin header, 4 pins [form="♀ (female)"]
  J141 = female pin header, 2 pins [form="♀ (female)"]
  J110 = female pin header, 4 pins [form="♀ (female)"]
  J3 = screw terminal, 2 pins
  R60 = Resistor [tolerance=±5% resistance=220 package=THT]
  IC4 = IC, DIP package, 16 pins [chip_label=SP720]

nets (from the pcb view):
  N1: Arduino_Mega_2560.A8, R22.Pin_1, C10.1, IC4.pin2
  N2: Arduino_Mega_2560.A0, R2.Pin_1, C2.1, IC4.pin15
  N3: Arduino_Mega_2560.A1, R4.Pin_1, C4.1, IC4.pin14
  N4: Arduino_Mega_2560.A2, R6.Pin_1, C6.1, IC4.pin1
  N5: Arduino_Mega_2560.A3, C18.0, R41.Pin_1, J4.pin11
  N6: Arduino_Mega_2560.A4, R8.Pin_1, C8.0, IC4.pin13
  N7: Arduino_Mega_2560.D21/SCL, Arduino_Mega_2560.SCL, J128.pin1
  N8: Arduino_Mega_2560.D20/SDA, Arduino_Mega_2560.SDA, J129.pin1
  N9: Arduino_Mega_2560.D19/RX1, IC3.pin8, R59.Pin_1, C25.0, IC4.pin3
  N10: Arduino_Mega_2560.D18/TX1, IC3.pin7, C24.0, R60.Pin_1
  N11: Arduino_Mega_2560.D17_PWM/RX2, DRV8825.STEP
  N12: Arduino_Mega_2560.D16_PWM/TX2, DRV8825.DIR
  N13: Arduino_Mega_2560.D13_PWM, J144.pin1
  N14: Arduino_Mega_2560.D12_PWM, J143.pin1
  N15: Arduino_Mega_2560.D11_PWM, R16.Pin_0, R14.Pin_0
  N16: Arduino_Mega_2560.D10_PWM, R15.Pin_0, R13.Pin_0
  N17: Arduino_Mega_2560.D9_PWM, R12.Pin_0, R10.Pin_0
  N18: Arduino_Mega_2560.D8_PWM, R11.Pin_0, R9.Pin_0
  N19: Arduino_Mega_2560.RESET, D17.anode, C23.1, J142.pin2
  N20: Arduino_Mega_2560.5V, R1.Pin_0, R3.Pin_0, U1.output_voltage, C14.+, C13.1, IC3.pin5, JP1.pin1, R39.Pin_0, R40.Pin_0, C19.1, C20.1, D16.cathode, D17.cathode, J4.pin13, J4.pin28, DRV8825.RESET, DRV8825.SLEEP, R61.Pin_1, MPX4250AP1.Vs, R54.Pin_1, R62.Pin_1, J109.pin1, J109.pin2, J109.pin3, J109.pin4, IC4.pin16
  N21: Arduino_Mega_2560.D0_RX0, J76.pin1
  N22: Arduino_Mega_2560.D1_TX0, J50.pin1
  N23: Arduino_Mega_2560.D2_PWM, R61.Pin_0, J114.pin1
  N24: Arduino_Mega_2560.D3_PWM, J145.pin1
  N25: Arduino_Mega_2560.D4_PWM, R58.Pin_0
  N26: Arduino_Mega_2560.D5_PWM, R50.Pin_0
  N27: Arduino_Mega_2560.D6_PWM, R57.Pin_0
  N28: Arduino_Mega_2560.D7_PWM, R51.Pin_0
  N29: Arduino_Mega_2560.D24, DRV8825.ENABLE
  N30: Arduino_Mega_2560.D38, R24.Pin_0
  N31: Arduino_Mega_2560.D40, R23.Pin_0
  N32: Arduino_Mega_2560.D43, J60.pin1, 12v_Jump.In_2
  N33: Arduino_Mega_2560.D45, J62.pin1, 12v_Jump.In_4
  N34: Arduino_Mega_2560.D47, J68.pin1, 12v_Jump.In_3
  N35: Arduino_Mega_2560.D49, J58.pin1, 12v_Jump.In_5
  N36: Arduino_Mega_2560.D50, R30.Pin_0
  N37: Arduino_Mega_2560.D51, J4.pin18, J57.pin1
  N38: Arduino_Mega_2560.D52, R29.Pin_0
  N39: R1.Pin_1, R2.Pin_0, C1.1, J4.pin20
  N40: R3.Pin_1, R4.Pin_0, C3.1, J4.pin19
  N41: R6.Pin_0, C5.1, J4.pin22
  N42: R7.Pin_0, D15.anode, C15.1, C16.+, U2.P$1, JP1.pin3, DRV8825.VMOT, 12v_Jump.COM_-_Common, R63.Pin_1, J140.pin1, J140.pin2, J3.pin2
  N43: R7.Pin_1, R8.Pin_0, C7.1, R21.Pin_0
  N44: Q1.gate, R11.Pin_1
  N45: Q1.drain, J4.pin1, J4.pin40
  N46: Q2.gate, R15.Pin_1
  N47: Q2.drain, J4.pin3, J4.pin4
  N48: Q3.gate, R12.Pin_1
  N49: Q3.drain, J4.pin2, J4.pin39
  N50: Q4.gate, R16.Pin_1
  N51: Q4.drain, J4.pin5, J4.pin6
  N52: C9.1, R22.Pin_0, J4.pin21
  N53: IC1.pin2, R23.Pin_1, R37.Pin_1
  N54: IC1.pin4, R24.Pin_1, R35.Pin_1
  N55: IC1.pin5, R25.Pin_0
  N56: IC1.pin6, C11.1, IC2.pin6, C12.1, JP1.pin2
  N57: IC1.pin7, R27.Pin_1
  N58: R25.Pin_1, R26.Pin_1, J4.pin34
  N59: R26.Pin_0, LED2.anode
  N60: R27.Pin_0, R28.Pin_1, J4.pin7
  N61: R28.Pin_0, LED1.anode
  N62: IC2.pin2, R29.Pin_1, R38.Pin_1
  N63: IC2.pin4, R30.Pin_1, R36.Pin_1
  N64: IC2.pin5, R32.Pin_0
  N65: IC2.pin7, R31.Pin_1
  N66: R33.Pin_0, LED3.anode
  N67: R33.Pin_1, J4.pin33, R31.Pin_0
  N68: R34.Pin_0, LED4.anode
  N69: R34.Pin_1, R32.Pin_1, J4.pin8
  N70: U1.input_voltage, D15.cathode
  N71: IC3.pin1, J4.pin27
  N72: IC3.pin2, JP2.pin3
  N73: IC3.pin3, JP3.pin1
  N74: IC3.pin4, J4.pin26
  N75: JP2.pin1, R59.Pin_0
  N76: JP2.pin2, JP4.pin2, J4.pin25
  N77: JP3.pin2, JP5.pin1, J4.pin24
  N78: JP3.pin3, R60.Pin_0
  N79: R39.Pin_1, JP4.pin1
  N80: R40.Pin_1, JP5.pin2
  N81: C18.1, C19.0, J4.pin9, J4.pin10, J4.pin12
  N82: R41.Pin_0, MPX4250AP1.V_out
  N83: R48.Pin_1, R50.Pin_1, Q7.gate
  N84: R49.Pin_1, R51.Pin_1, Q8.gate
  N85: R55.Pin_1, R57.Pin_1, Q5.gate
  N86: R56.Pin_1, R58.Pin_1, Q6.gate
  N87: Q5.drain, J4.pin36
  N88: Q7.drain, J4.pin37
  N89: Q6.drain, J4.pin38
  N90: J4.pin14, 12v_Jump.Out_2
  N91: J4.pin15, 12v_Jump.Out_3
  N92: J4.pin16, 12v_Jump.Out_4
  N93: J4.pin17, 12v_Jump.Out_5, R63.Pin_0
  N94: J4.pin29, DRV8825.2B
  N95: J4.pin30, DRV8825.2A
  N96: J4.pin31, DRV8825.1A
  N97: J4.pin32, DRV8825.1B
  N98: J4.pin35, Q8.drain
  N99: J142.pin1, R54.Pin_0
  N100: J142.pin3, R62.Pin_0
  N101: J141.pin1, J141.pin2
  N102: J110.pin1, J110.pin2, J110.pin3, J110.pin4

notes:
  Inlet Air Temperature sensor
  Coolant Temperature Sensor
  Speeduino v0.4, Throttle Position Sensor
  Battery Reference Voltage
  Injector 1
  Speeduino v0.4, Connector 1
  Injector 3
  Injector 2
  Injector 4
  Speeduino v0.4, O2 Sensor
  Ignitor output 1
  Ignitor output 2
  12v
  5v
  Power supply
  IGN Out
  Crank and Cam sensors
  Speeduino v0.4, MAP sensor input
  DetonationEMS.com
  Generic Outputs - High Current
  inj1
  VR
  Hall
  Reset Protection - Refer AVR040 Application note
  ADC Clamping circuit
  Stepper Driver
  PWM Idle / Boost
  GND
  12V |
  51
  49
  45
  47
  43
  Proto Area
  Flat side down
  ULN2003a
  →
  Eth
  RX
  TX
  20 21
  5v   |
  |   GND  |
  | GND |
  Run  Prog
  D12 D13
  D3
  v1.1
  Aaron S. 2020
